// Logisim project Computer.circ as structural Verilog: 33 circuits, main circuit Half_Adder
module Half_Adder (
  input  Bit_1,
  input  Bit_2,
  output Sum,
  output Carry_Out
);

  xor xor_1 (Sum, Bit_1, Bit_2);
  and and_1 (Carry_Out, Bit_1, Bit_2);
endmodule

module Full_Adder (
  input  Carry_In,
  input  Bit_1,
  input  Bit_2,
  output Sum,
  output Carry_Out
);

  wire half_adder_1_carry_out, half_adder_1_sum, half_adder_2_carry_out;

  Half_Adder half_adder_1 (.Bit_1(Bit_1), .Bit_2(Bit_2), .Sum(half_adder_1_sum), .Carry_Out(half_adder_1_carry_out));
  Half_Adder half_adder_2 (.Bit_1(Carry_In), .Bit_2(half_adder_1_sum), .Sum(Sum), .Carry_Out(half_adder_2_carry_out));
  or or_1 (Carry_Out, half_adder_2_carry_out, half_adder_1_carry_out);
endmodule

module Byte_Adder (
  input  Carry_In,
  input  [7:0] A,
  input  [7:0] B,
  output [7:0] Sum,
  output Carry_Out
);

  wire full_adder_1_carry_out, full_adder_2_carry_out, full_adder_3_carry_out, full_adder_4_carry_out,
       full_adder_5_carry_out, full_adder_6_carry_out, full_adder_7_carry_out;

  Full_Adder full_adder_1 (
    .Carry_In(Carry_In), .Bit_1(A[0]), .Bit_2(B[0]), .Sum(Sum[0]), .Carry_Out(full_adder_1_carry_out));
  Full_Adder full_adder_2 (
    .Carry_In(full_adder_1_carry_out), .Bit_1(A[1]), .Bit_2(B[1]), .Sum(Sum[1]),
    .Carry_Out(full_adder_2_carry_out));
  Full_Adder full_adder_3 (
    .Carry_In(full_adder_2_carry_out), .Bit_1(A[2]), .Bit_2(B[2]), .Sum(Sum[2]),
    .Carry_Out(full_adder_3_carry_out));
  Full_Adder full_adder_4 (
    .Carry_In(full_adder_3_carry_out), .Bit_1(A[3]), .Bit_2(B[3]), .Sum(Sum[3]),
    .Carry_Out(full_adder_4_carry_out));
  Full_Adder full_adder_5 (
    .Carry_In(full_adder_4_carry_out), .Bit_1(A[4]), .Bit_2(B[4]), .Sum(Sum[4]),
    .Carry_Out(full_adder_5_carry_out));
  Full_Adder full_adder_6 (
    .Carry_In(full_adder_5_carry_out), .Bit_1(A[5]), .Bit_2(B[5]), .Sum(Sum[5]),
    .Carry_Out(full_adder_6_carry_out));
  Full_Adder full_adder_7 (
    .Carry_In(full_adder_6_carry_out), .Bit_1(A[6]), .Bit_2(B[6]), .Sum(Sum[6]),
    .Carry_Out(full_adder_7_carry_out));
  Full_Adder full_adder_8 (
    .Carry_In(full_adder_7_carry_out), .Bit_1(A[7]), .Bit_2(B[7]), .Sum(Sum[7]), .Carry_Out(Carry_Out));
  Three_Digit_Decimal_Integer_Display three_digit_decimal_integer_display_1 (.Binary_Number(Sum));
endmodule

module Byte_Register (
  input  Set,
  input  [7:0] Data,
  input  Clock,
  input  Reset,
  output [7:0] Normal_Output,
  output [7:0] Inverted_Output
);

  D_Flip_Flop d_ff_1 (
    .D(Data[0]), .clk(Clock), .Q(Normal_Output[0]), .Qn(Inverted_Output[0]), .preset(Set), .reset(Reset));
  D_Flip_Flop d_ff_2 (
    .D(Data[1]), .clk(Clock), .Q(Normal_Output[6]), .Qn(Inverted_Output[1]), .preset(Set), .reset(Reset));
  D_Flip_Flop d_ff_3 (
    .D(Data[2]), .clk(Clock), .Q(Normal_Output[5]), .Qn(Inverted_Output[2]), .preset(Set), .reset(Reset));
  D_Flip_Flop d_ff_4 (
    .D(Data[3]), .clk(Clock), .Q(Normal_Output[4]), .Qn(Inverted_Output[3]), .preset(Set), .reset(Reset));
  D_Flip_Flop d_ff_5 (
    .D(Data[4]), .clk(Clock), .Q(Normal_Output[3]), .Qn(Inverted_Output[4]), .preset(Set), .reset(Reset));
  D_Flip_Flop d_ff_6 (
    .D(Data[5]), .clk(Clock), .Q(Normal_Output[2]), .Qn(Inverted_Output[5]), .preset(Set), .reset(Reset));
  D_Flip_Flop d_ff_7 (
    .D(Data[6]), .clk(Clock), .Q(Normal_Output[1]), .Qn(Inverted_Output[6]), .preset(Set), .reset(Reset));
  D_Flip_Flop d_ff_8 (
    .D(Data[7]), .clk(Clock), .Q(Normal_Output[7]), .Qn(Inverted_Output[7]), .preset(Set), .reset(Reset));
endmodule

module Seven_Segment_Display_Driver (
  input  Bit_0,
  input  Bit_1,
  input  Bit_2,
  input  Bit_3,
  input  Decimal_Point,
  output B,
  output A,
  output F,
  output G,
  output E,
  output D,
  output C,
  output DP
);

  wire and_1_out, and_2_out, and_3_out, and_4_out, and_5_out, and_6_out, and_7_out, and_8_out, and_9_out,
       and_10_out, and_11_out, and_12_out, and_13_out, and_14_out, and_15_out, and_16_out, and_17_out,
       and_18_out, and_19_out, and_20_out, and_21_out, and_22_out, and_23_out, and_24_out, and_25_out,
       and_26_out, and_27_out, and_28_out, and_29_out, and_30_out, and_31_out, and_32_out, and_33_out,
       and_34_out, not_1_out, not_2_out, not_3_out, not_4_out;

  not not_1 (not_1_out, Bit_3);
  not not_2 (not_2_out, Bit_2);
  not not_3 (not_3_out, Bit_1);
  not not_4 (not_4_out, Bit_0);
  and and_1 (and_1_out, not_1_out, not_2_out);
  and and_2 (and_2_out, Bit_3, not_3_out, Bit_0);
  and and_3 (and_3_out, not_1_out, Bit_1, Bit_0);
  and and_4 (and_4_out, not_1_out, not_3_out, not_4_out);
  and and_5 (and_5_out, Bit_3, not_2_out, not_4_out);
  and and_6 (and_6_out, Bit_1, not_4_out);
  and and_7 (and_7_out, not_1_out, Bit_1);
  and and_8 (and_8_out, Bit_2, Bit_1);
  and and_9 (and_9_out, not_1_out, Bit_2, Bit_0);
  and and_10 (and_10_out, Bit_3, not_2_out, not_3_out);
  and and_11 (and_11_out, not_1_out, not_2_out, not_4_out);
  and and_12 (and_12_out, Bit_3, not_2_out);
  and and_13 (and_13_out, Bit_3, Bit_1);
  and and_14 (and_14_out, not_1_out, Bit_2, not_3_out);
  and and_15 (and_15_out, not_1_out, not_3_out, not_4_out);
  and and_16 (and_16_out, Bit_2, Bit_1, not_4_out);
  and and_17 (and_17_out, Bit_1, not_4_out);
  and and_18 (and_18_out, not_2_out, Bit_1);
  and and_19 (and_19_out, Bit_2, not_3_out);
  and and_20 (and_20_out, Bit_3, Bit_2);
  and and_21 (and_21_out, Bit_1, not_4_out);
  and and_22 (and_22_out, Bit_3, Bit_1);
  and and_23 (and_23_out, not_2_out, not_4_out);
  and and_24 (and_24_out, Bit_3, not_3_out);
  and and_25 (and_25_out, Bit_2, Bit_1, not_4_out);
  and and_26 (and_26_out, not_1_out, not_2_out, Bit_1);
  and and_27 (and_27_out, not_1_out, not_2_out, not_4_out);
  and and_28 (and_28_out, Bit_2, not_3_out, Bit_0);
  and and_29 (and_29_out, Bit_3, not_2_out, Bit_0);
  and and_30 (and_30_out, Bit_3, not_2_out);
  and and_31 (and_31_out, not_3_out, Bit_0);
  and and_32 (and_32_out, not_1_out, Bit_2);
  and and_33 (and_33_out, not_1_out, not_3_out);
  and and_34 (and_34_out, not_1_out, Bit_0);
  or or_1 (B, and_1_out, and_2_out, and_3_out, and_4_out, and_5_out);
  or or_2 (A, and_6_out, and_7_out, and_8_out, and_9_out, and_10_out, and_11_out);
  or or_3 (F, and_12_out, and_13_out, and_14_out, and_15_out, and_16_out);
  or or_4 (G, and_17_out, and_18_out, and_19_out, Bit_3);
  or or_5 (E, and_20_out, and_21_out, and_22_out, and_23_out);
  or or_6 (D, and_24_out, and_25_out, and_26_out, and_27_out, and_28_out, and_29_out);
  or or_7 (C, and_30_out, and_31_out, and_32_out, and_33_out, and_34_out);

  assign DP = Decimal_Point;
endmodule

module Seven_Segment_Display_Driver_with_Enable_Bit (
  input  Bit_0,
  input  Bit_1,
  input  Bit_2,
  input  Bit_3,
  input  Enable,
  input  Decimal_Point,
  output B,
  output A,
  output F,
  output G,
  output E,
  output D,
  output C,
  output DP
);

  wire and_1_out, and_2_out, and_3_out, and_4_out, and_5_out, and_6_out, and_7_out, and_8_out, and_9_out,
       and_10_out, and_11_out, and_12_out, and_13_out, and_14_out, and_15_out, and_16_out, and_17_out,
       and_18_out, and_19_out, and_20_out, and_21_out, and_22_out, and_23_out, and_24_out, and_25_out,
       and_26_out, and_27_out, and_28_out, and_29_out, and_30_out, and_31_out, and_32_out, and_33_out,
       and_34_out, not_1_out, not_2_out, not_3_out, not_4_out, not_5_out, or_1_out, or_2_out, or_3_out,
       or_4_out, or_5_out, or_6_out;

  not not_1 (not_1_out, Bit_3);
  not not_2 (not_2_out, Bit_2);
  not not_3 (not_3_out, Bit_1);
  not not_4 (not_4_out, Bit_0);
  and and_1 (and_1_out, not_1_out, not_2_out);
  and and_2 (and_2_out, Bit_3, not_3_out, Bit_0);
  and and_3 (and_3_out, not_1_out, Bit_1, Bit_0);
  and and_4 (and_4_out, not_1_out, not_3_out, not_4_out);
  and and_5 (and_5_out, Bit_3, not_2_out, not_4_out);
  and and_6 (and_6_out, Bit_1, not_4_out);
  and and_7 (and_7_out, not_1_out, Bit_1);
  and and_8 (and_8_out, Bit_2, Bit_1);
  and and_9 (and_9_out, not_1_out, Bit_2, Bit_0);
  and and_10 (and_10_out, Bit_3, not_2_out, not_3_out);
  and and_11 (and_11_out, not_1_out, not_2_out, not_4_out);
  and and_12 (and_12_out, Bit_3, not_2_out);
  and and_13 (and_13_out, Bit_3, Bit_1);
  and and_14 (and_14_out, not_1_out, Bit_2, not_3_out);
  and and_15 (and_15_out, not_1_out, not_3_out, not_4_out);
  and and_16 (and_16_out, Bit_2, Bit_1, not_4_out);
  and and_17 (and_17_out, Bit_1, not_4_out);
  and and_18 (and_18_out, not_2_out, Bit_1);
  and and_19 (and_19_out, Bit_2, not_3_out);
  and and_20 (and_20_out, Bit_3, Bit_2);
  and and_21 (and_21_out, Bit_1, not_4_out);
  and and_22 (and_22_out, Bit_3, Bit_1);
  and and_23 (and_23_out, not_2_out, not_4_out);
  and and_24 (and_24_out, Bit_3, not_3_out);
  and and_25 (and_25_out, Bit_2, Bit_1, not_4_out);
  and and_26 (and_26_out, not_1_out, not_2_out, Bit_1);
  and and_27 (and_27_out, not_1_out, not_2_out, not_4_out);
  and and_28 (and_28_out, Bit_2, not_3_out, Bit_0);
  and and_29 (and_29_out, Bit_3, not_2_out, Bit_0);
  and and_30 (and_30_out, Bit_3, not_2_out);
  and and_31 (and_31_out, not_3_out, Bit_0);
  and and_32 (and_32_out, not_1_out, Bit_2);
  and and_33 (and_33_out, not_1_out, not_3_out);
  and and_34 (and_34_out, not_1_out, Bit_0);
  or or_1 (or_1_out, and_1_out, and_2_out, and_3_out, and_4_out, and_5_out);
  or or_2 (or_2_out, and_6_out, and_7_out, and_8_out, and_9_out, and_10_out, and_11_out);
  or or_3 (or_3_out, and_12_out, and_13_out, and_14_out, and_15_out, and_16_out);
  or or_4 (or_4_out, and_20_out, and_21_out, and_22_out, and_23_out);
  or or_5 (or_5_out, and_24_out, and_25_out, and_26_out, and_27_out, and_28_out, and_29_out);
  or or_6 (or_6_out, and_30_out, and_31_out, and_32_out, and_33_out, and_34_out);
  and and_35 (B, or_1_out, Enable);
  and and_36 (A, or_2_out, Enable);
  and and_37 (F, or_3_out, Enable);
  not not_5 (not_5_out, Enable);
  or or_7 (G, and_17_out, and_18_out, not_5_out, and_19_out, Bit_3);
  and and_38 (E, or_4_out, Enable);
  and and_39 (D, or_5_out, Enable);
  and and_40 (C, or_6_out, Enable);
  and and_41 (DP, Enable, Decimal_Point);
endmodule

module SSDDriver (
  input  D3,
  input  D2,
  input  D1,
  input  D0,
  output A,
  output B,
  output C,
  output D,
  output E,
  output F,
  output G,
  output DP
);

  wire nand_1_out, nand_2_out, nand_3_out, nand_4_out, nand_5_out, nand_6_out, nand_7_out, nand_8_out,
       nand_9_out, nand_10_out, nand_11_out, nand_12_out, nand_13_out, nand_14_out, nand_15_out, nand_16_out,
       nand_17_out, nand_18_out, nand_19_out, nand_20_out, nand_21_out, nand_22_out, nand_23_out,
       nand_24_out, nand_25_out, nand_26_out, nand_27_out, nand_28_out, nand_29_out, nand_30_out,
       nand_31_out, nand_32_out, nand_33_out, nand_34_out, nand_35_out, nand_36_out, nand_37_out,
       nand_38_out, nand_39_out, nand_40_out, nand_41_out, nand_42_out, nand_43_out, nand_44_out,
       nand_45_out, nand_46_out, nand_47_out, nand_48_out, nand_49_out, nand_50_out, nand_51_out,
       nand_52_out, nand_53_out, nand_54_out, nand_55_out, nand_56_out, nand_57_out, nand_58_out,
       nand_59_out, nand_60_out, nand_61_out, nand_62_out, nand_63_out, nand_64_out, nand_66_out,
       nand_67_out, nand_68_out, nand_69_out, nand_70_out, nand_71_out, nand_72_out, nand_73_out,
       nand_74_out, nand_75_out, nand_76_out, nand_77_out, nand_78_out, nand_79_out, nand_80_out,
       nand_81_out, nand_82_out, nand_83_out, nand_84_out, nand_85_out, nand_86_out, nand_87_out,
       nand_88_out, nand_89_out, nand_90_out, nand_91_out, nand_92_out, nand_94_out, nand_95_out,
       nand_96_out, nand_97_out, nand_99_out, nand_100_out, nand_101_out, nand_102_out, nand_103_out,
       nand_104_out, nand_105_out, nand_106_out;

  nand nand_1 (nand_1_out, 1'b1, D3);
  nand nand_2 (nand_2_out, 1'b1, D2);
  nand nand_3 (nand_3_out, 1'b1, D1);
  nand nand_4 (nand_4_out, 1'b1, D0);
  nand nand_5 (nand_5_out, D3, nand_2_out);
  nand nand_6 (nand_6_out, nand_1_out, nand_3_out);
  nand nand_7 (nand_7_out, nand_1_out, D1);
  nand nand_8 (nand_8_out, nand_1_out, D2);
  nand nand_9 (nand_9_out, D3, nand_2_out);
  nand nand_10 (nand_10_out, D2, nand_3_out);
  nand nand_11 (nand_11_out, nand_1_out, nand_2_out);
  nand nand_12 (nand_12_out, nand_2_out, nand_4_out);
  nand nand_13 (nand_13_out, D1, nand_4_out);
  nand nand_14 (nand_14_out, D3, D1);
  nand nand_15 (nand_15_out, D3, D2);
  nand nand_16 (nand_16_out, nand_1_out, D2);
  nand nand_17 (nand_17_out, nand_2_out, D1);
  nand nand_18 (nand_18_out, D3, nand_2_out);
  nand nand_19 (nand_19_out, nand_1_out, D2);
  nand nand_20 (nand_20_out, nand_5_out, nand_5_out);
  nand nand_21 (nand_21_out, nand_6_out, nand_6_out);
  nand nand_22 (nand_22_out, nand_7_out, nand_7_out);
  nand nand_23 (nand_23_out, nand_8_out, nand_9_out);
  nand nand_24 (nand_24_out, nand_10_out, nand_10_out);
  nand nand_25 (nand_25_out, nand_11_out, nand_11_out);
  nand nand_26 (nand_26_out, nand_12_out, nand_13_out);
  nand nand_27 (nand_27_out, nand_14_out, nand_15_out);
  nand nand_28 (nand_28_out, nand_16_out, nand_16_out);
  nand nand_29 (nand_29_out, nand_17_out, nand_18_out);
  nand nand_30 (nand_30_out, nand_19_out, nand_19_out);
  nand nand_31 (nand_31_out, nand_2_out, nand_4_out);
  nand nand_32 (nand_32_out, nand_1_out, D1);
  nand nand_33 (nand_33_out, nand_1_out, D2);
  nand nand_34 (nand_34_out, nand_20_out, nand_3_out);
  nand nand_35 (nand_35_out, D3, nand_4_out);
  nand nand_36 (nand_36_out, nand_21_out, nand_4_out);
  nand nand_37 (nand_37_out, nand_22_out, D0);
  nand nand_38 (nand_38_out, D3, nand_3_out);
  nand nand_39 (nand_39_out, nand_23_out, nand_23_out);
  nand nand_40 (nand_40_out, nand_3_out, D0);
  nand nand_41 (nand_41_out, nand_2_out, nand_3_out);
  nand nand_42 (nand_42_out, nand_2_out, D0);
  nand nand_43 (nand_43_out, nand_24_out, D0);
  nand nand_44 (nand_44_out, nand_25_out, nand_4_out);
  nand nand_45 (nand_45_out, nand_2_out, D1);
  nand nand_46 (nand_46_out, D2, D1);
  nand nand_47 (nand_47_out, nand_26_out, nand_26_out);
  nand nand_48 (nand_48_out, nand_27_out, nand_27_out);
  nand nand_49 (nand_49_out, nand_3_out, nand_4_out);
  nand nand_50 (nand_50_out, nand_28_out, nand_3_out);
  nand nand_51 (nand_51_out, nand_29_out, nand_29_out);
  nand nand_52 (nand_52_out, nand_30_out, nand_3_out);
  nand nand_53 (nand_53_out, D1, nand_4_out);
  nand nand_54 (nand_54_out, D3, D0);
  nand nand_55 (nand_55_out, nand_31_out, nand_32_out);
  nand nand_56 (nand_56_out, nand_33_out, nand_33_out);
  nand nand_57 (nand_57_out, nand_34_out, nand_35_out);
  nand nand_58 (nand_58_out, nand_36_out, nand_37_out);
  nand nand_59 (nand_59_out, nand_38_out, nand_38_out);
  nand nand_60 (nand_60_out, nand_39_out, nand_40_out);
  nand nand_61 (nand_61_out, nand_41_out, nand_42_out);
  nand nand_62 (nand_62_out, nand_43_out, nand_44_out);
  nand nand_63 (nand_63_out, nand_45_out, nand_45_out);
  nand nand_64 (nand_64_out, nand_46_out, nand_46_out);
  nand nand_65 (E, nand_47_out, nand_48_out);
  nand nand_66 (nand_66_out, nand_49_out, nand_50_out);
  nand nand_67 (nand_67_out, nand_51_out, nand_52_out);
  nand nand_68 (nand_68_out, nand_53_out, nand_54_out);
  nand nand_69 (nand_69_out, nand_55_out, nand_55_out);
  nand nand_70 (nand_70_out, nand_56_out, D0);
  nand nand_71 (nand_71_out, nand_57_out, nand_57_out);
  nand nand_72 (nand_72_out, D2, D1);
  nand nand_73 (nand_73_out, nand_58_out, nand_58_out);
  nand nand_74 (nand_74_out, nand_2_out, nand_4_out);
  nand nand_75 (nand_75_out, nand_59_out, D0);
  nand nand_76 (nand_76_out, nand_1_out, nand_2_out);
  nand nand_77 (nand_77_out, nand_60_out, nand_60_out);
  nand nand_78 (nand_78_out, nand_61_out, nand_61_out);
  nand nand_79 (nand_79_out, nand_62_out, nand_62_out);
  nand nand_80 (nand_80_out, nand_63_out, D0);
  nand nand_81 (nand_81_out, D3, nand_3_out);
  nand nand_82 (nand_82_out, nand_64_out, nand_4_out);
  nand nand_83 (nand_83_out, nand_66_out, nand_66_out);
  nand nand_84 (nand_84_out, D2, nand_4_out);
  nand nand_85 (nand_85_out, D3, nand_2_out);
  nand nand_86 (nand_86_out, D3, D1);
  nand nand_87 (nand_87_out, nand_67_out, nand_67_out);
  nand nand_88 (nand_88_out, nand_68_out, nand_68_out);
  nand nand_89 (nand_89_out, nand_69_out, nand_70_out);
  nand nand_90 (nand_90_out, nand_71_out, nand_72_out);
  nand nand_91 (nand_91_out, nand_73_out, nand_74_out);
  nand nand_92 (nand_92_out, nand_75_out, nand_76_out);
  nand nand_93 (C, nand_77_out, nand_78_out);
  nand nand_94 (nand_94_out, nand_79_out, nand_80_out);
  nand nand_95 (nand_95_out, nand_81_out, nand_82_out);
  nand nand_96 (nand_96_out, nand_83_out, nand_84_out);
  nand nand_97 (nand_97_out, nand_85_out, nand_86_out);
  nand nand_98 (G, nand_87_out, nand_88_out);
  nand nand_99 (nand_99_out, nand_89_out, nand_89_out);
  nand nand_100 (nand_100_out, nand_90_out, nand_90_out);
  nand nand_101 (nand_101_out, nand_91_out, nand_91_out);
  nand nand_102 (nand_102_out, nand_92_out, nand_92_out);
  nand nand_103 (nand_103_out, nand_94_out, nand_94_out);
  nand nand_104 (nand_104_out, nand_95_out, nand_95_out);
  nand nand_105 (nand_105_out, nand_96_out, nand_96_out);
  nand nand_106 (nand_106_out, nand_97_out, nand_97_out);
  nand nand_107 (A, nand_99_out, nand_100_out);
  nand nand_108 (B, nand_101_out, nand_102_out);
  nand nand_109 (D, nand_103_out, nand_104_out);
  nand nand_110 (F, nand_105_out, nand_106_out);

  assign DP = 1'b0;
endmodule

module One_Digit_Hexadecimal_Display (
  input  [3:0] Nibble
);

  wire seven_segment_display_driver_1_a, seven_segment_display_driver_1_b, seven_segment_display_driver_1_c,
       seven_segment_display_driver_1_d, seven_segment_display_driver_1_e, seven_segment_display_driver_1_f,
       seven_segment_display_driver_1_g;

  Seven_Segment_Display_Driver seven_segment_display_driver_1 (
    .Bit_0(Nibble[0]), .Bit_1(Nibble[1]), .Bit_2(Nibble[2]), .Bit_3(Nibble[3]),
    .B(seven_segment_display_driver_1_b), .A(seven_segment_display_driver_1_a),
    .F(seven_segment_display_driver_1_f), .G(seven_segment_display_driver_1_g),
    .E(seven_segment_display_driver_1_e), .D(seven_segment_display_driver_1_d),
    .C(seven_segment_display_driver_1_c));  // open: Decimal_Point, DP
  _7_Segment_Display u_7_segment_display_1 (
    .g(seven_segment_display_driver_1_g), .f(seven_segment_display_driver_1_f),
    .a(seven_segment_display_driver_1_a), .b(seven_segment_display_driver_1_b),
    .e(seven_segment_display_driver_1_e), .d(seven_segment_display_driver_1_d),
    .c(seven_segment_display_driver_1_c));  // open: dp
endmodule

module Two_Digit_Hexadecimal_Display (
  input  [7:0] Byte
);

  wire seven_segment_display_driver_1_a, seven_segment_display_driver_1_b, seven_segment_display_driver_1_c,
       seven_segment_display_driver_1_d, seven_segment_display_driver_1_e, seven_segment_display_driver_1_f,
       seven_segment_display_driver_1_g, seven_segment_display_driver_2_a, seven_segment_display_driver_2_b,
       seven_segment_display_driver_2_c, seven_segment_display_driver_2_d, seven_segment_display_driver_2_e,
       seven_segment_display_driver_2_f, seven_segment_display_driver_2_g;

  Seven_Segment_Display_Driver seven_segment_display_driver_1 (
    .Bit_0(Byte[0]), .Bit_1(Byte[1]), .Bit_2(Byte[2]), .Bit_3(Byte[3]), .B(seven_segment_display_driver_1_b),
    .A(seven_segment_display_driver_1_a), .F(seven_segment_display_driver_1_f),
    .G(seven_segment_display_driver_1_g), .E(seven_segment_display_driver_1_e),
    .D(seven_segment_display_driver_1_d), .C(seven_segment_display_driver_1_c));  // open: Decimal_Point, DP
  Seven_Segment_Display_Driver seven_segment_display_driver_2 (
    .Bit_0(Byte[4]), .Bit_1(Byte[5]), .Bit_2(Byte[6]), .Bit_3(Byte[7]), .B(seven_segment_display_driver_2_b),
    .A(seven_segment_display_driver_2_a), .F(seven_segment_display_driver_2_f),
    .G(seven_segment_display_driver_2_g), .E(seven_segment_display_driver_2_e),
    .D(seven_segment_display_driver_2_d), .C(seven_segment_display_driver_2_c));  // open: Decimal_Point, DP
  _7_Segment_Display u_7_segment_display_1 (
    .g(seven_segment_display_driver_2_g), .f(seven_segment_display_driver_2_f),
    .a(seven_segment_display_driver_2_a), .b(seven_segment_display_driver_2_b),
    .e(seven_segment_display_driver_2_e), .d(seven_segment_display_driver_2_d),
    .c(seven_segment_display_driver_2_c));  // open: dp
  _7_Segment_Display u_7_segment_display_2 (
    .g(seven_segment_display_driver_1_g), .f(seven_segment_display_driver_1_f),
    .a(seven_segment_display_driver_1_a), .b(seven_segment_display_driver_1_b),
    .e(seven_segment_display_driver_1_e), .d(seven_segment_display_driver_1_d),
    .c(seven_segment_display_driver_1_c));  // open: dp
endmodule

module Two_Digit_Hexadecimal_Display_With_Enable_Bit (
  input  [7:0] Byte,
  input  Enable
);

  wire seven_segment_display_driver_with_enable_bit_1_a, seven_segment_display_driver_with_enable_bit_1_b,
       seven_segment_display_driver_with_enable_bit_1_c, seven_segment_display_driver_with_enable_bit_1_d,
       seven_segment_display_driver_with_enable_bit_1_e, seven_segment_display_driver_with_enable_bit_1_f,
       seven_segment_display_driver_with_enable_bit_1_g, seven_segment_display_driver_with_enable_bit_2_a,
       seven_segment_display_driver_with_enable_bit_2_b, seven_segment_display_driver_with_enable_bit_2_c,
       seven_segment_display_driver_with_enable_bit_2_d, seven_segment_display_driver_with_enable_bit_2_e,
       seven_segment_display_driver_with_enable_bit_2_f, seven_segment_display_driver_with_enable_bit_2_g;

  Seven_Segment_Display_Driver_with_Enable_Bit seven_segment_display_driver_with_enable_bit_1 (
    .Bit_0(Byte[0]), .Bit_1(Byte[1]), .Bit_2(Byte[2]), .Bit_3(Byte[3]), .Enable(Enable),
    .B(seven_segment_display_driver_with_enable_bit_1_b),
    .A(seven_segment_display_driver_with_enable_bit_1_a),
    .F(seven_segment_display_driver_with_enable_bit_1_f),
    .G(seven_segment_display_driver_with_enable_bit_1_g),
    .E(seven_segment_display_driver_with_enable_bit_1_e),
    .D(seven_segment_display_driver_with_enable_bit_1_d), .C(seven_segment_display_driver_with_enable_bit_1_c));  // open: Decimal_Point, DP
  Seven_Segment_Display_Driver_with_Enable_Bit seven_segment_display_driver_with_enable_bit_2 (
    .Bit_0(Byte[4]), .Bit_1(Byte[5]), .Bit_2(Byte[6]), .Bit_3(Byte[7]), .Enable(Enable),
    .B(seven_segment_display_driver_with_enable_bit_2_b),
    .A(seven_segment_display_driver_with_enable_bit_2_a),
    .F(seven_segment_display_driver_with_enable_bit_2_f),
    .G(seven_segment_display_driver_with_enable_bit_2_g),
    .E(seven_segment_display_driver_with_enable_bit_2_e),
    .D(seven_segment_display_driver_with_enable_bit_2_d), .C(seven_segment_display_driver_with_enable_bit_2_c));  // open: Decimal_Point, DP
  _7_Segment_Display u_7_segment_display_1 (
    .g(seven_segment_display_driver_with_enable_bit_2_g),
    .f(seven_segment_display_driver_with_enable_bit_2_f),
    .a(seven_segment_display_driver_with_enable_bit_2_a),
    .b(seven_segment_display_driver_with_enable_bit_2_b),
    .e(seven_segment_display_driver_with_enable_bit_2_e),
    .d(seven_segment_display_driver_with_enable_bit_2_d), .c(seven_segment_display_driver_with_enable_bit_2_c));  // open: dp
  _7_Segment_Display u_7_segment_display_2 (
    .g(seven_segment_display_driver_with_enable_bit_1_g),
    .f(seven_segment_display_driver_with_enable_bit_1_f),
    .a(seven_segment_display_driver_with_enable_bit_1_a),
    .b(seven_segment_display_driver_with_enable_bit_1_b),
    .e(seven_segment_display_driver_with_enable_bit_1_e),
    .d(seven_segment_display_driver_with_enable_bit_1_d), .c(seven_segment_display_driver_with_enable_bit_1_c));  // open: dp
endmodule

module Three_Digit_Decimal_Integer_Display (
  input  [7:0] Binary_Number
);

  wire double_dabble_1_hundreds0, double_dabble_1_hundreds1, double_dabble_1_hundreds2,
       double_dabble_1_hundreds3, double_dabble_1_ones0, double_dabble_1_ones1, double_dabble_1_ones2,
       double_dabble_1_ones3, double_dabble_1_tens0, double_dabble_1_tens1, double_dabble_1_tens2,
       double_dabble_1_tens3, seven_segment_display_driver_1_a, seven_segment_display_driver_1_b,
       seven_segment_display_driver_1_c, seven_segment_display_driver_1_d, seven_segment_display_driver_1_e,
       seven_segment_display_driver_1_f, seven_segment_display_driver_1_g, seven_segment_display_driver_2_a,
       seven_segment_display_driver_2_b, seven_segment_display_driver_2_c, seven_segment_display_driver_2_d,
       seven_segment_display_driver_2_e, seven_segment_display_driver_2_f, seven_segment_display_driver_2_g,
       seven_segment_display_driver_3_a, seven_segment_display_driver_3_b, seven_segment_display_driver_3_c,
       seven_segment_display_driver_3_d, seven_segment_display_driver_3_e, seven_segment_display_driver_3_f,
       seven_segment_display_driver_3_g;

  Double_Dabble double_dabble_1 (
    .Data(Binary_Number), .Ones0(double_dabble_1_ones0), .Ones1(double_dabble_1_ones1),
    .Ones2(double_dabble_1_ones2), .Ones3(double_dabble_1_ones3), .Tens0(double_dabble_1_tens0),
    .Tens1(double_dabble_1_tens1), .Tens2(double_dabble_1_tens2), .Tens3(double_dabble_1_tens3),
    .Hundreds0(double_dabble_1_hundreds0), .Hundreds1(double_dabble_1_hundreds1),
    .Hundreds2(double_dabble_1_hundreds2), .Hundreds3(double_dabble_1_hundreds3));
  Seven_Segment_Display_Driver seven_segment_display_driver_1 (
    .Bit_0(double_dabble_1_ones0), .Bit_1(double_dabble_1_ones1), .Bit_2(double_dabble_1_ones2),
    .Bit_3(double_dabble_1_ones3), .B(seven_segment_display_driver_1_b),
    .A(seven_segment_display_driver_1_a), .F(seven_segment_display_driver_1_f),
    .G(seven_segment_display_driver_1_g), .E(seven_segment_display_driver_1_e),
    .D(seven_segment_display_driver_1_d), .C(seven_segment_display_driver_1_c));  // open: Decimal_Point, DP
  Seven_Segment_Display_Driver seven_segment_display_driver_2 (
    .Bit_0(double_dabble_1_tens0), .Bit_1(double_dabble_1_tens1), .Bit_2(double_dabble_1_tens2),
    .Bit_3(double_dabble_1_tens3), .B(seven_segment_display_driver_2_b),
    .A(seven_segment_display_driver_2_a), .F(seven_segment_display_driver_2_f),
    .G(seven_segment_display_driver_2_g), .E(seven_segment_display_driver_2_e),
    .D(seven_segment_display_driver_2_d), .C(seven_segment_display_driver_2_c));  // open: Decimal_Point, DP
  Seven_Segment_Display_Driver seven_segment_display_driver_3 (
    .Bit_0(double_dabble_1_hundreds0), .Bit_1(double_dabble_1_hundreds1), .Bit_2(double_dabble_1_hundreds2),
    .Bit_3(double_dabble_1_hundreds3), .B(seven_segment_display_driver_3_b),
    .A(seven_segment_display_driver_3_a), .F(seven_segment_display_driver_3_f),
    .G(seven_segment_display_driver_3_g), .E(seven_segment_display_driver_3_e),
    .D(seven_segment_display_driver_3_d), .C(seven_segment_display_driver_3_c));  // open: Decimal_Point, DP
  _7_Segment_Display u_7_segment_display_1 (
    .g(seven_segment_display_driver_3_g), .f(seven_segment_display_driver_3_f),
    .a(seven_segment_display_driver_3_a), .b(seven_segment_display_driver_3_b),
    .e(seven_segment_display_driver_3_e), .d(seven_segment_display_driver_3_d),
    .c(seven_segment_display_driver_3_c));  // open: dp
  _7_Segment_Display u_7_segment_display_2 (
    .g(seven_segment_display_driver_2_g), .f(seven_segment_display_driver_2_f),
    .a(seven_segment_display_driver_2_a), .b(seven_segment_display_driver_2_b),
    .e(seven_segment_display_driver_2_e), .d(seven_segment_display_driver_2_d),
    .c(seven_segment_display_driver_2_c));  // open: dp
  _7_Segment_Display u_7_segment_display_3 (
    .g(seven_segment_display_driver_1_g), .f(seven_segment_display_driver_1_f),
    .a(seven_segment_display_driver_1_a), .b(seven_segment_display_driver_1_b),
    .e(seven_segment_display_driver_1_e), .d(seven_segment_display_driver_1_d),
    .c(seven_segment_display_driver_1_c));  // open: dp
endmodule

module Three_Digit_Decimal_Integer_Display_with_Enable_Bit (
  input  [7:0] Binary_Number,
  input  Enable
);

  wire double_dabble_1_hundreds0, double_dabble_1_hundreds1, double_dabble_1_hundreds2,
       double_dabble_1_hundreds3, double_dabble_1_ones0, double_dabble_1_ones1, double_dabble_1_ones2,
       double_dabble_1_ones3, double_dabble_1_tens0, double_dabble_1_tens1, double_dabble_1_tens2,
       double_dabble_1_tens3, seven_segment_display_driver_with_enable_bit_1_a,
       seven_segment_display_driver_with_enable_bit_1_b, seven_segment_display_driver_with_enable_bit_1_c,
       seven_segment_display_driver_with_enable_bit_1_d, seven_segment_display_driver_with_enable_bit_1_e,
       seven_segment_display_driver_with_enable_bit_1_f, seven_segment_display_driver_with_enable_bit_1_g,
       seven_segment_display_driver_with_enable_bit_2_a, seven_segment_display_driver_with_enable_bit_2_b,
       seven_segment_display_driver_with_enable_bit_2_c, seven_segment_display_driver_with_enable_bit_2_d,
       seven_segment_display_driver_with_enable_bit_2_e, seven_segment_display_driver_with_enable_bit_2_f,
       seven_segment_display_driver_with_enable_bit_2_g, seven_segment_display_driver_with_enable_bit_3_a,
       seven_segment_display_driver_with_enable_bit_3_b, seven_segment_display_driver_with_enable_bit_3_c,
       seven_segment_display_driver_with_enable_bit_3_d, seven_segment_display_driver_with_enable_bit_3_e,
       seven_segment_display_driver_with_enable_bit_3_f, seven_segment_display_driver_with_enable_bit_3_g;

  Double_Dabble double_dabble_1 (
    .Data(Binary_Number), .Ones0(double_dabble_1_ones0), .Ones1(double_dabble_1_ones1),
    .Ones2(double_dabble_1_ones2), .Ones3(double_dabble_1_ones3), .Tens0(double_dabble_1_tens0),
    .Tens1(double_dabble_1_tens1), .Tens2(double_dabble_1_tens2), .Tens3(double_dabble_1_tens3),
    .Hundreds0(double_dabble_1_hundreds0), .Hundreds1(double_dabble_1_hundreds1),
    .Hundreds2(double_dabble_1_hundreds2), .Hundreds3(double_dabble_1_hundreds3));
  Seven_Segment_Display_Driver_with_Enable_Bit seven_segment_display_driver_with_enable_bit_1 (
    .Bit_0(double_dabble_1_ones0), .Bit_1(double_dabble_1_ones1), .Bit_2(double_dabble_1_ones2),
    .Bit_3(double_dabble_1_ones3), .Enable(Enable), .B(seven_segment_display_driver_with_enable_bit_1_b),
    .A(seven_segment_display_driver_with_enable_bit_1_a),
    .F(seven_segment_display_driver_with_enable_bit_1_f),
    .G(seven_segment_display_driver_with_enable_bit_1_g),
    .E(seven_segment_display_driver_with_enable_bit_1_e),
    .D(seven_segment_display_driver_with_enable_bit_1_d), .C(seven_segment_display_driver_with_enable_bit_1_c));  // open: Decimal_Point, DP
  Seven_Segment_Display_Driver_with_Enable_Bit seven_segment_display_driver_with_enable_bit_2 (
    .Bit_0(double_dabble_1_tens0), .Bit_1(double_dabble_1_tens1), .Bit_2(double_dabble_1_tens2),
    .Bit_3(double_dabble_1_tens3), .Enable(Enable), .B(seven_segment_display_driver_with_enable_bit_2_b),
    .A(seven_segment_display_driver_with_enable_bit_2_a),
    .F(seven_segment_display_driver_with_enable_bit_2_f),
    .G(seven_segment_display_driver_with_enable_bit_2_g),
    .E(seven_segment_display_driver_with_enable_bit_2_e),
    .D(seven_segment_display_driver_with_enable_bit_2_d), .C(seven_segment_display_driver_with_enable_bit_2_c));  // open: Decimal_Point, DP
  Seven_Segment_Display_Driver_with_Enable_Bit seven_segment_display_driver_with_enable_bit_3 (
    .Bit_0(double_dabble_1_hundreds0), .Bit_1(double_dabble_1_hundreds1), .Bit_2(double_dabble_1_hundreds2),
    .Bit_3(double_dabble_1_hundreds3), .Enable(Enable), .B(seven_segment_display_driver_with_enable_bit_3_b),
    .A(seven_segment_display_driver_with_enable_bit_3_a),
    .F(seven_segment_display_driver_with_enable_bit_3_f),
    .G(seven_segment_display_driver_with_enable_bit_3_g),
    .E(seven_segment_display_driver_with_enable_bit_3_e),
    .D(seven_segment_display_driver_with_enable_bit_3_d), .C(seven_segment_display_driver_with_enable_bit_3_c));  // open: Decimal_Point, DP
  _7_Segment_Display u_7_segment_display_1 (
    .g(seven_segment_display_driver_with_enable_bit_3_g),
    .f(seven_segment_display_driver_with_enable_bit_3_f),
    .a(seven_segment_display_driver_with_enable_bit_3_a),
    .b(seven_segment_display_driver_with_enable_bit_3_b),
    .e(seven_segment_display_driver_with_enable_bit_3_e),
    .d(seven_segment_display_driver_with_enable_bit_3_d), .c(seven_segment_display_driver_with_enable_bit_3_c));  // open: dp
  _7_Segment_Display u_7_segment_display_2 (
    .g(seven_segment_display_driver_with_enable_bit_2_g),
    .f(seven_segment_display_driver_with_enable_bit_2_f),
    .a(seven_segment_display_driver_with_enable_bit_2_a),
    .b(seven_segment_display_driver_with_enable_bit_2_b),
    .e(seven_segment_display_driver_with_enable_bit_2_e),
    .d(seven_segment_display_driver_with_enable_bit_2_d), .c(seven_segment_display_driver_with_enable_bit_2_c));  // open: dp
  _7_Segment_Display u_7_segment_display_3 (
    .g(seven_segment_display_driver_with_enable_bit_1_g),
    .f(seven_segment_display_driver_with_enable_bit_1_f),
    .a(seven_segment_display_driver_with_enable_bit_1_a),
    .b(seven_segment_display_driver_with_enable_bit_1_b),
    .e(seven_segment_display_driver_with_enable_bit_1_e),
    .d(seven_segment_display_driver_with_enable_bit_1_d), .c(seven_segment_display_driver_with_enable_bit_1_c));  // open: dp
endmodule

module Double_Dabble_Nibble_Adder (
  input  Carry_In,
  input  A0,
  input  A1,
  input  A2,
  input  A3,
  output Sum0,
  output Sum1,
  output Sum2,
  output Sum3,
  output Carry_Out
);

  wire and_1_out, and_2_out, and_3_out, and_4_out, and_5_out, and_6_out, and_7_out, full_adder_1_carry_out,
       full_adder_2_carry_out, full_adder_3_carry_out, half_adder_1_carry_out;

  and and_1 (and_1_out, A2, A1);
  and and_2 (and_2_out, A2, A0);
  or or_1 (Carry_Out, A3, and_1_out, and_2_out);
  and and_3 (and_3_out, Carry_Out, 1'b0);
  and and_4 (and_4_out, Carry_Out, 1'b1);
  and and_5 (and_5_out, Carry_Out, 1'b1);
  and and_6 (and_6_out, Carry_Out, 1'b0);
  and and_7 (and_7_out, Carry_Out, 1'b1);
  Half_Adder half_adder_1 (.Bit_1(Carry_In), .Bit_2(and_3_out), .Sum(Sum0), .Carry_Out(half_adder_1_carry_out));
  Full_Adder full_adder_1 (
    .Carry_In(half_adder_1_carry_out), .Bit_1(A0), .Bit_2(and_4_out), .Sum(Sum1),
    .Carry_Out(full_adder_1_carry_out));
  Full_Adder full_adder_2 (
    .Carry_In(full_adder_1_carry_out), .Bit_1(A1), .Bit_2(and_5_out), .Sum(Sum2),
    .Carry_Out(full_adder_2_carry_out));
  Full_Adder full_adder_3 (
    .Carry_In(full_adder_2_carry_out), .Bit_1(A2), .Bit_2(and_6_out), .Sum(Sum3),
    .Carry_Out(full_adder_3_carry_out));
  Full_Adder full_adder_4 (.Carry_In(full_adder_3_carry_out), .Bit_1(A3), .Bit_2(and_7_out));  // open: Sum, Carry_Out
endmodule

module Double_Dabble (
  input  [7:0] Data,
  output Ones0,
  output Ones1,
  output Ones2,
  output Ones3,
  output Tens0,
  output Tens1,
  output Tens2,
  output Tens3,
  output Hundreds0,
  output Hundreds1,
  output Hundreds2,
  output Hundreds3
);

  wire double_dabble_nibble_adder_1_carry_out, double_dabble_nibble_adder_1_sum0,
       double_dabble_nibble_adder_1_sum1, double_dabble_nibble_adder_1_sum2,
       double_dabble_nibble_adder_1_sum3, double_dabble_nibble_adder_2_sum0,
       double_dabble_nibble_adder_2_sum1, double_dabble_nibble_adder_2_sum2,
       double_dabble_nibble_adder_2_sum3, double_dabble_nibble_adder_3_carry_out,
       double_dabble_nibble_adder_3_sum0, double_dabble_nibble_adder_3_sum1,
       double_dabble_nibble_adder_3_sum2, double_dabble_nibble_adder_3_sum3,
       double_dabble_nibble_adder_4_carry_out, double_dabble_nibble_adder_4_sum0,
       double_dabble_nibble_adder_4_sum1, double_dabble_nibble_adder_4_sum2,
       double_dabble_nibble_adder_4_sum3, double_dabble_nibble_adder_5_sum0,
       double_dabble_nibble_adder_5_sum1, double_dabble_nibble_adder_5_sum2,
       double_dabble_nibble_adder_5_sum3, double_dabble_nibble_adder_6_sum0,
       double_dabble_nibble_adder_6_sum1, double_dabble_nibble_adder_6_sum2,
       double_dabble_nibble_adder_6_sum3, double_dabble_nibble_adder_7_carry_out,
       double_dabble_nibble_adder_7_sum0, double_dabble_nibble_adder_7_sum1,
       double_dabble_nibble_adder_7_sum2, double_dabble_nibble_adder_7_sum3,
       double_dabble_nibble_adder_8_carry_out, double_dabble_nibble_adder_8_sum0,
       double_dabble_nibble_adder_8_sum1, double_dabble_nibble_adder_8_sum2,
       double_dabble_nibble_adder_8_sum3, double_dabble_nibble_adder_9_sum0,
       double_dabble_nibble_adder_9_sum1, double_dabble_nibble_adder_9_sum2,
       double_dabble_nibble_adder_9_sum3, double_dabble_nibble_adder_10_carry_out,
       double_dabble_nibble_adder_11_carry_out;

  Double_Dabble_Nibble_Adder double_dabble_nibble_adder_1 (
    .Carry_In(Data[4]), .A0(Data[5]), .A1(Data[6]), .A2(Data[7]), .A3(1'b0),
    .Sum0(double_dabble_nibble_adder_1_sum0), .Sum1(double_dabble_nibble_adder_1_sum1),
    .Sum2(double_dabble_nibble_adder_1_sum2), .Sum3(double_dabble_nibble_adder_1_sum3),
    .Carry_Out(double_dabble_nibble_adder_1_carry_out));
  Double_Dabble_Nibble_Adder double_dabble_nibble_adder_2 (
    .Carry_In(double_dabble_nibble_adder_1_carry_out), .A0(1'b0), .A1(1'b0), .A2(1'b0), .A3(1'b0),
    .Sum0(double_dabble_nibble_adder_2_sum0), .Sum1(double_dabble_nibble_adder_2_sum1),
    .Sum2(double_dabble_nibble_adder_2_sum2), .Sum3(double_dabble_nibble_adder_2_sum3));  // open: Carry_Out
  Double_Dabble_Nibble_Adder double_dabble_nibble_adder_3 (
    .Carry_In(Data[2]), .A0(double_dabble_nibble_adder_4_sum0), .A1(double_dabble_nibble_adder_4_sum1),
    .A2(double_dabble_nibble_adder_4_sum2), .A3(double_dabble_nibble_adder_4_sum3),
    .Sum0(double_dabble_nibble_adder_3_sum0), .Sum1(double_dabble_nibble_adder_3_sum1),
    .Sum2(double_dabble_nibble_adder_3_sum2), .Sum3(double_dabble_nibble_adder_3_sum3),
    .Carry_Out(double_dabble_nibble_adder_3_carry_out));
  Double_Dabble_Nibble_Adder double_dabble_nibble_adder_4 (
    .Carry_In(Data[3]), .A0(double_dabble_nibble_adder_1_sum0), .A1(double_dabble_nibble_adder_1_sum1),
    .A2(double_dabble_nibble_adder_1_sum2), .A3(double_dabble_nibble_adder_1_sum3),
    .Sum0(double_dabble_nibble_adder_4_sum0), .Sum1(double_dabble_nibble_adder_4_sum1),
    .Sum2(double_dabble_nibble_adder_4_sum2), .Sum3(double_dabble_nibble_adder_4_sum3),
    .Carry_Out(double_dabble_nibble_adder_4_carry_out));
  Double_Dabble_Nibble_Adder double_dabble_nibble_adder_5 (
    .Carry_In(double_dabble_nibble_adder_3_carry_out), .A0(double_dabble_nibble_adder_6_sum0),
    .A1(double_dabble_nibble_adder_6_sum1), .A2(double_dabble_nibble_adder_6_sum2),
    .A3(double_dabble_nibble_adder_6_sum3), .Sum0(double_dabble_nibble_adder_5_sum0),
    .Sum1(double_dabble_nibble_adder_5_sum1), .Sum2(double_dabble_nibble_adder_5_sum2),
    .Sum3(double_dabble_nibble_adder_5_sum3));  // open: Carry_Out
  Double_Dabble_Nibble_Adder double_dabble_nibble_adder_6 (
    .Carry_In(double_dabble_nibble_adder_4_carry_out), .A0(double_dabble_nibble_adder_2_sum0),
    .A1(double_dabble_nibble_adder_2_sum1), .A2(double_dabble_nibble_adder_2_sum2),
    .A3(double_dabble_nibble_adder_2_sum3), .Sum0(double_dabble_nibble_adder_6_sum0),
    .Sum1(double_dabble_nibble_adder_6_sum1), .Sum2(double_dabble_nibble_adder_6_sum2),
    .Sum3(double_dabble_nibble_adder_6_sum3));  // open: Carry_Out
  Double_Dabble_Nibble_Adder double_dabble_nibble_adder_7 (
    .Carry_In(Data[1]), .A0(double_dabble_nibble_adder_3_sum0), .A1(double_dabble_nibble_adder_3_sum1),
    .A2(double_dabble_nibble_adder_3_sum2), .A3(double_dabble_nibble_adder_3_sum3),
    .Sum0(double_dabble_nibble_adder_7_sum0), .Sum1(double_dabble_nibble_adder_7_sum1),
    .Sum2(double_dabble_nibble_adder_7_sum2), .Sum3(double_dabble_nibble_adder_7_sum3),
    .Carry_Out(double_dabble_nibble_adder_7_carry_out));
  Double_Dabble_Nibble_Adder double_dabble_nibble_adder_8 (
    .Carry_In(double_dabble_nibble_adder_7_carry_out), .A0(double_dabble_nibble_adder_5_sum0),
    .A1(double_dabble_nibble_adder_5_sum1), .A2(double_dabble_nibble_adder_5_sum2),
    .A3(double_dabble_nibble_adder_5_sum3), .Sum0(double_dabble_nibble_adder_8_sum0),
    .Sum1(double_dabble_nibble_adder_8_sum1), .Sum2(double_dabble_nibble_adder_8_sum2),
    .Sum3(double_dabble_nibble_adder_8_sum3), .Carry_Out(double_dabble_nibble_adder_8_carry_out));
  Double_Dabble_Nibble_Adder double_dabble_nibble_adder_9 (
    .Carry_In(double_dabble_nibble_adder_8_carry_out), .A0(1'b0), .A1(1'b0), .A2(1'b0), .A3(1'b0),
    .Sum0(double_dabble_nibble_adder_9_sum0), .Sum1(double_dabble_nibble_adder_9_sum1),
    .Sum2(double_dabble_nibble_adder_9_sum2), .Sum3(double_dabble_nibble_adder_9_sum3));  // open: Carry_Out
  Double_Dabble_Nibble_Adder double_dabble_nibble_adder_10 (
    .Carry_In(Data[0]), .A0(double_dabble_nibble_adder_7_sum0), .A1(double_dabble_nibble_adder_7_sum1),
    .A2(double_dabble_nibble_adder_7_sum2), .A3(double_dabble_nibble_adder_7_sum3), .Sum0(Ones0),
    .Sum1(Ones1), .Sum2(Ones2), .Sum3(Ones3), .Carry_Out(double_dabble_nibble_adder_10_carry_out));
  Double_Dabble_Nibble_Adder double_dabble_nibble_adder_11 (
    .Carry_In(double_dabble_nibble_adder_10_carry_out), .A0(double_dabble_nibble_adder_8_sum0),
    .A1(double_dabble_nibble_adder_8_sum1), .A2(double_dabble_nibble_adder_8_sum2),
    .A3(double_dabble_nibble_adder_8_sum3), .Sum0(Tens0), .Sum1(Tens1), .Sum2(Tens2), .Sum3(Tens3),
    .Carry_Out(double_dabble_nibble_adder_11_carry_out));
  Double_Dabble_Nibble_Adder double_dabble_nibble_adder_12 (
    .Carry_In(double_dabble_nibble_adder_11_carry_out), .A0(double_dabble_nibble_adder_9_sum0),
    .A1(double_dabble_nibble_adder_9_sum1), .A2(double_dabble_nibble_adder_9_sum2),
    .A3(double_dabble_nibble_adder_9_sum3), .Sum0(Hundreds0), .Sum1(Hundreds1), .Sum2(Hundreds2),
    .Sum3(Hundreds3));  // open: Carry_Out
endmodule

module Dabble (
  input  D3,
  input  D2,
  input  D1,
  input  D0,
  output O3,
  output O2,
  output O1,
  output O0
);

  wire nand_1_out, nand_2_out, nand_3_out, nand_4_out, nand_5_out, nand_6_out, nand_7_out, nand_8_out,
       nand_9_out, nand_10_out, nand_11_out, nand_12_out, nand_13_out, nand_14_out, nand_15_out, nand_16_out,
       nand_17_out, nand_18_out, nand_19_out, nand_20_out, nand_21_out, nand_22_out, nand_23_out,
       nand_25_out, nand_26_out, nand_27_out, nand_28_out, nand_29_out, nand_30_out, nand_31_out,
       nand_32_out, nand_33_out, nand_34_out;

  nand nand_1 (nand_1_out, 1'b1, D3);
  nand nand_2 (nand_2_out, 1'b1, D2);
  nand nand_3 (nand_3_out, 1'b1, D1);
  nand nand_4 (nand_4_out, 1'b1, D0);
  nand nand_5 (nand_5_out, D2, D0);
  nand nand_6 (nand_6_out, D2, D1);
  nand nand_7 (nand_7_out, D2, nand_3_out);
  nand nand_8 (nand_8_out, nand_1_out, nand_2_out);
  nand nand_9 (nand_9_out, nand_1_out, nand_2_out);
  nand nand_10 (nand_10_out, D2, D1);
  nand nand_11 (nand_11_out, nand_5_out, nand_6_out);
  nand nand_12 (nand_12_out, nand_7_out, nand_7_out);
  nand nand_13 (nand_13_out, nand_8_out, nand_8_out);
  nand nand_14 (nand_14_out, nand_9_out, nand_9_out);
  nand nand_15 (nand_15_out, nand_10_out, nand_10_out);
  nand nand_16 (nand_16_out, nand_11_out, nand_11_out);
  nand nand_17 (nand_17_out, nand_12_out, nand_4_out);
  nand nand_18 (nand_18_out, D3, D0);
  nand nand_19 (nand_19_out, nand_13_out, D1);
  nand nand_20 (nand_20_out, D1, D0);
  nand nand_21 (nand_21_out, D3, nand_3_out);
  nand nand_22 (nand_22_out, nand_14_out, D0);
  nand nand_23 (nand_23_out, nand_15_out, nand_4_out);
  nand nand_24 (O3, nand_16_out, nand_1_out);
  nand nand_25 (nand_25_out, nand_17_out, nand_18_out);
  nand nand_26 (nand_26_out, nand_19_out, nand_20_out);
  nand nand_27 (nand_27_out, nand_21_out, nand_21_out);
  nand nand_28 (nand_28_out, nand_22_out, nand_23_out);
  nand nand_29 (nand_29_out, nand_25_out, nand_25_out);
  nand nand_30 (nand_30_out, D3, D1);
  nand nand_31 (nand_31_out, nand_26_out, nand_26_out);
  nand nand_32 (nand_32_out, nand_27_out, nand_4_out);
  nand nand_33 (nand_33_out, nand_28_out, nand_28_out);
  nand nand_34 (nand_34_out, D3, nand_4_out);
  nand nand_35 (O2, nand_29_out, nand_30_out);
  nand nand_36 (O1, nand_31_out, nand_32_out);
  nand nand_37 (O0, nand_33_out, nand_34_out);
endmodule

module DoubleDabble (
  input  D7,
  input  D6,
  input  D5,
  input  D4,
  input  D3,
  input  D2,
  input  D1,
  input  D0,
  output HUND3,
  output HUND2,
  output HUND1,
  output HUND0,
  output TENS3,
  output TENS2,
  output TENS1,
  output TENS0,
  output ONES3,
  output ONES2,
  output ONES1,
  output ONES0
);

  wire DAB_A_o0, DAB_A_o1, DAB_A_o2, DAB_A_o3, DAB_B_o0, DAB_B_o1, DAB_B_o2, DAB_B_o3, DAB_C_o0, DAB_C_o1,
       DAB_C_o2, DAB_C_o3, DAB_D_o0, DAB_D_o1, DAB_D_o2, DAB_E_o0, DAB_E_o1, DAB_E_o2, DAB_E_o3;

  Dabble DAB_A (.D3(1'b0), .D2(D7), .D1(D6), .D0(D5), .O3(DAB_A_o3), .O2(DAB_A_o2), .O1(DAB_A_o1), .O0(DAB_A_o0));
  Dabble DAB_B (
    .D3(DAB_A_o2), .D2(DAB_A_o1), .D1(DAB_A_o0), .D0(D4), .O3(DAB_B_o3), .O2(DAB_B_o2), .O1(DAB_B_o1),
    .O0(DAB_B_o0));
  Dabble DAB_C (
    .D3(DAB_B_o2), .D2(DAB_B_o1), .D1(DAB_B_o0), .D0(D3), .O3(DAB_C_o3), .O2(DAB_C_o2), .O1(DAB_C_o1),
    .O0(DAB_C_o0));
  Dabble DAB_D (
    .D3(1'b0), .D2(DAB_A_o3), .D1(DAB_B_o3), .D0(DAB_C_o3), .O3(HUND1), .O2(DAB_D_o2), .O1(DAB_D_o1),
    .O0(DAB_D_o0));
  Dabble DAB_E (
    .D3(DAB_C_o2), .D2(DAB_C_o1), .D1(DAB_C_o0), .D0(D2), .O3(DAB_E_o3), .O2(DAB_E_o2), .O1(DAB_E_o1),
    .O0(DAB_E_o0));
  Dabble DAB_F (
    .D3(DAB_D_o2), .D2(DAB_D_o1), .D1(DAB_D_o0), .D0(DAB_E_o3), .O3(HUND0), .O2(TENS3), .O1(TENS2), .O0(TENS1));
  Dabble DAB_G (.D3(DAB_E_o2), .D2(DAB_E_o1), .D1(DAB_E_o0), .D0(D1), .O3(TENS0), .O2(ONES3), .O1(ONES2), .O0(ONES1));

  assign HUND2 = 1'b0;
  assign HUND3 = 1'b0;
  assign ONES0 = D0;
endmodule

module SSD8Bits (
);

  wire dipswitch_1_p1, dipswitch_1_p2, dipswitch_1_p3, dipswitch_1_p4, dipswitch_1_p5, dipswitch_1_p6,
       dipswitch_1_p7, dipswitch_1_p8, doubledabble_1_hund0, doubledabble_1_hund1, doubledabble_1_hund2,
       doubledabble_1_hund3, doubledabble_1_ones0, doubledabble_1_ones1, doubledabble_1_ones2,
       doubledabble_1_ones3, doubledabble_1_tens0, doubledabble_1_tens1, doubledabble_1_tens2,
       doubledabble_1_tens3, ssddriver_1_a, ssddriver_1_b, ssddriver_1_c, ssddriver_1_d, ssddriver_1_dp,
       ssddriver_1_e, ssddriver_1_f, ssddriver_1_g, ssddriver_2_a, ssddriver_2_b, ssddriver_2_c,
       ssddriver_2_d, ssddriver_2_dp, ssddriver_2_e, ssddriver_2_f, ssddriver_2_g, ssddriver_3_a,
       ssddriver_3_b, ssddriver_3_c, ssddriver_3_d, ssddriver_3_dp, ssddriver_3_e, ssddriver_3_f,
       ssddriver_3_g;

  SSDDriver ssddriver_1 (
    .D3(doubledabble_1_hund3), .D2(doubledabble_1_hund2), .D1(doubledabble_1_hund1),
    .D0(doubledabble_1_hund0), .A(ssddriver_1_a), .B(ssddriver_1_b), .C(ssddriver_1_c), .D(ssddriver_1_d),
    .E(ssddriver_1_e), .F(ssddriver_1_f), .G(ssddriver_1_g), .DP(ssddriver_1_dp));
  _7_Segment_Display u_7_segment_display_1 (
    .g(ssddriver_1_g), .f(ssddriver_1_f), .a(ssddriver_1_a), .b(ssddriver_1_b), .e(ssddriver_1_e),
    .d(ssddriver_1_d), .c(ssddriver_1_c), .dp(ssddriver_1_dp));
  _7_Segment_Display u_7_segment_display_2 (
    .g(ssddriver_2_g), .f(ssddriver_2_f), .a(ssddriver_2_a), .b(ssddriver_2_b), .e(ssddriver_2_e),
    .d(ssddriver_2_d), .c(ssddriver_2_c), .dp(ssddriver_2_dp));
  // DipSwitch dipswitch_1: pin names not known; wires that end beside it: dipswitch_1_p1, dipswitch_1_p2, dipswitch_1_p3, dipswitch_1_p4, dipswitch_1_p5, dipswitch_1_p6, dipswitch_1_p7, dipswitch_1_p8
  DoubleDabble doubledabble_1 (
    .D7(dipswitch_1_p8), .D6(dipswitch_1_p7), .D5(dipswitch_1_p6), .D4(dipswitch_1_p5), .D3(dipswitch_1_p4),
    .D2(dipswitch_1_p3), .D1(dipswitch_1_p2), .D0(dipswitch_1_p1), .HUND3(doubledabble_1_hund3),
    .HUND2(doubledabble_1_hund2), .HUND1(doubledabble_1_hund1), .HUND0(doubledabble_1_hund0),
    .TENS3(doubledabble_1_tens3), .TENS2(doubledabble_1_tens2), .TENS1(doubledabble_1_tens1),
    .TENS0(doubledabble_1_tens0), .ONES3(doubledabble_1_ones3), .ONES2(doubledabble_1_ones2),
    .ONES1(doubledabble_1_ones1), .ONES0(doubledabble_1_ones0));
  SSDDriver ssddriver_2 (
    .D3(doubledabble_1_tens3), .D2(doubledabble_1_tens2), .D1(doubledabble_1_tens1),
    .D0(doubledabble_1_tens0), .A(ssddriver_2_a), .B(ssddriver_2_b), .C(ssddriver_2_c), .D(ssddriver_2_d),
    .E(ssddriver_2_e), .F(ssddriver_2_f), .G(ssddriver_2_g), .DP(ssddriver_2_dp));
  _7_Segment_Display u_7_segment_display_3 (
    .g(ssddriver_3_g), .f(ssddriver_3_f), .a(ssddriver_3_a), .b(ssddriver_3_b), .e(ssddriver_3_e),
    .d(ssddriver_3_d), .c(ssddriver_3_c), .dp(ssddriver_3_dp));
  SSDDriver ssddriver_3 (
    .D3(doubledabble_1_ones3), .D2(doubledabble_1_ones2), .D1(doubledabble_1_ones1),
    .D0(doubledabble_1_ones0), .A(ssddriver_3_a), .B(ssddriver_3_b), .C(ssddriver_3_c), .D(ssddriver_3_d),
    .E(ssddriver_3_e), .F(ssddriver_3_f), .G(ssddriver_3_g), .DP(ssddriver_3_dp));

  // Notes on the sheet:
  //   Hundreds
  //   DoubleDabble
  //   Tens
  //   Ones
endmodule

module Negate_Byte (
  input  [7:0] Input_Byte,
  input  Negate_Signal,
  output [7:0] Output_Byte
);

  xor xor_1 (Output_Byte[0], Negate_Signal, Input_Byte[0]);
  xor xor_2 (Output_Byte[1], Negate_Signal, Input_Byte[1]);
  xor xor_3 (Output_Byte[2], Negate_Signal, Input_Byte[2]);
  xor xor_4 (Output_Byte[3], Negate_Signal, Input_Byte[3]);
  xor xor_5 (Output_Byte[4], Negate_Signal, Input_Byte[4]);
  xor xor_6 (Output_Byte[5], Negate_Signal, Input_Byte[5]);
  xor xor_7 (Output_Byte[6], Negate_Signal, Input_Byte[6]);
  xor xor_8 (Output_Byte[7], Input_Byte[7], Negate_Signal);
endmodule

module Inverter8Bits (
  input  [7:0] Input_Byte,
  input  Invert,
  output [7:0] Output_Byte
);

  xor xor_1 (Output_Byte[0], Input_Byte[0], Invert);
  xor xor_2 (Output_Byte[1], Input_Byte[1], Invert);
  xor xor_3 (Output_Byte[2], Input_Byte[2], Invert);
  xor xor_4 (Output_Byte[3], Input_Byte[3], Invert);
  xor xor_5 (Output_Byte[4], Input_Byte[4], Invert);
  xor xor_6 (Output_Byte[5], Input_Byte[5], Invert);
  xor xor_7 (Output_Byte[6], Input_Byte[6], Invert);
  xor xor_8 (Output_Byte[7], Input_Byte[7], Invert);
endmodule

module ALU (
  input  Read_Enable,
  input  Carry_In,
  input  [7:0] A,
  input  [7:0] B,
  input  [2:0] Opcode,
  output [7:0] Result,
  output [2:0] Flags
);

  wire A_D, ADD, and_2_out, and_3_out, and_4_out, and_5_out, byte_adder_1_carry_out, N_T, O_R, or_1_out,
       or_2_out, SHL, SHR, SUB, X_R;
  wire [6:0] controlled_buffer_1_out;
  wire [7:0] and_1_out, byte_adder_1_sum, negate_byte_1_output_byte, not_1_out, or_3_out, xor_1_out;

  Decoder #(.enable("false"), .select(3)) decoder_1 (
    .out0(ADD), .out1(SUB), .out2(SHR), .out3(SHL), .out4(A_D), .out5(O_R), .out6(X_R), .out7(N_T),
    .sel(Opcode));
  LED ADD_Light (.in(ADD));
  LED SUB_Light (.in(SUB));
  LED AND_Light (.in(A_D));
  LED OR_Light (.in(O_R));
  LED XOR_Light (.in(X_R));
  LED NOT_Light (.in(N_T));
  LED SHR_Light (.in(SHR));
  LED SHL_Light (.in(SHL));
  Two_Digit_Hexadecimal_Display two_digit_hexadecimal_display_1 (.Byte(A));
  Two_Digit_Hexadecimal_Display two_digit_hexadecimal_display_2 (.Byte(B));
  or or_1 (or_1_out, Carry_In, SUB);
  Negate_Byte negate_byte_1 (.Input_Byte(B), .Negate_Signal(SUB), .Output_Byte(negate_byte_1_output_byte));
  or or_2 (or_2_out, ADD, SUB);
  Byte_Adder byte_adder_1 (
    .Carry_In(or_1_out), .A(A), .B(negate_byte_1_output_byte), .Sum(byte_adder_1_sum),
    .Carry_Out(byte_adder_1_carry_out));
  assign and_1_out = A & B;  // AND_Gate and_1, 8 bits wide
  assign or_3_out = A | B;  // OR_Gate or_3, 8 bits wide
  assign xor_1_out = A ^ B;  // XOR_Gate xor_1, 8 bits wide
  assign not_1_out = ~A;  // NOT_Gate not_1, 8 bits wide
  assign {Flags[1], controlled_buffer_1_out} = or_2_out ? byte_adder_1_sum : 8'bz;  // Controlled_Buffer_part controlled_buffer_1
  assign {Flags[1], controlled_buffer_1_out} = A_D ? and_1_out : 8'bz;  // Controlled_Buffer_part controlled_buffer_2
  assign {Flags[1], controlled_buffer_1_out} = O_R ? or_3_out : 8'bz;  // Controlled_Buffer_part controlled_buffer_3
  assign {Flags[1], controlled_buffer_1_out} = X_R ? xor_1_out : 8'bz;  // Controlled_Buffer_part controlled_buffer_4
  assign {Flags[1], controlled_buffer_1_out} = N_T ? not_1_out : 8'bz;  // Controlled_Buffer_part controlled_buffer_5
  assign {Flags[1], controlled_buffer_1_out} = SHR ? {Carry_In, A[7:1]} : 8'bz;  // Controlled_Buffer_part controlled_buffer_6
  assign {Flags[1], controlled_buffer_1_out} = SHL ? {A[6:0], Carry_In} : 8'bz;  // Controlled_Buffer_part controlled_buffer_7
  assign Result = Read_Enable ? {Flags[1], controlled_buffer_1_out} : 8'bz;  // Controlled_Buffer_part controlled_buffer_8
  Two_Digit_Hexadecimal_Display_With_Enable_Bit two_digit_hexadecimal_display_with_enable_bit_1 (
    .Byte(Result), .Enable(Read_Enable));
  and and_2 (and_2_out, ADD, byte_adder_1_carry_out);
  and and_3 (and_3_out, SUB, byte_adder_1_carry_out);
  and and_4 (and_4_out, SHR, A[0]);
  and and_5 (and_5_out, SHL, A[7]);
  or or_4 (Flags[2], and_2_out, and_3_out, and_4_out, and_5_out);
  nor nor_1 (Flags[0], controlled_buffer_1_out[0], controlled_buffer_1_out[1], controlled_buffer_1_out[2], controlled_buffer_1_out[3], controlled_buffer_1_out[4], controlled_buffer_1_out[5], controlled_buffer_1_out[6], Flags[1]);
  LED Zero_Flag_Light (.in(Flags[0]));
  LED Negative_Flag_Light (.in(Flags[1]));
  LED Carry_Flag_Light (.in(Flags[2]));

  // Other names for the same wires on the sheet: Cin = Carry_In
endmodule

module Controlled_Buffer (
  input  [7:0] Input_Byte,
  input  Connect_Input_Byte_to_Bus,
  input  Write_Enable,
  input  [1:0] Select_Register,
  input  Reset_Register_0,
  input  Reset_Register_1,
  input  Reset_Register_2,
  input  Reset_Register_3,
  input  Connect_Register_0_to_Bus,
  input  Connect_Register_1_to_Bus,
  input  Connect_Register_2_to_Bus,
  input  Connect_Register_3_to_Bus,
  output [7:0] Output_Byte
);

  wire demultiplexer_1_out0, demultiplexer_1_out1, demultiplexer_1_out2, demultiplexer_1_out3,
       Input_Clock_out;
  wire [7:0] Register_0_q, Register_1_q, Register_2_q, Register_3_q;

  assign Output_Byte = Connect_Input_Byte_to_Bus ? Input_Byte : 8'bz;  // Controlled_Buffer_part controlled_buffer_1
  Clock Input_Clock (.out(Input_Clock_out));
  Demultiplexer #(.select(2)) demultiplexer_1 (
    .out0(demultiplexer_1_out0), .out1(demultiplexer_1_out1), .out2(demultiplexer_1_out2),
    .out3(demultiplexer_1_out3), .in(Write_Enable), .sel(Select_Register));
  Register Register_0 (
    .D(Output_Byte), .en(demultiplexer_1_out0), .clk(Input_Clock_out), .Q(Register_0_q),
    .clr(Reset_Register_0));
  Register Register_1 (
    .D(Output_Byte), .en(demultiplexer_1_out1), .clk(Input_Clock_out), .Q(Register_1_q),
    .clr(Reset_Register_1));
  Register Register_2 (
    .D(Output_Byte), .en(demultiplexer_1_out2), .clk(Input_Clock_out), .Q(Register_2_q),
    .clr(Reset_Register_2));
  Register Register_3 (
    .D(Output_Byte), .en(demultiplexer_1_out3), .clk(Input_Clock_out), .Q(Register_3_q),
    .clr(Reset_Register_3));
  assign Output_Byte = Connect_Register_0_to_Bus ? Register_0_q : 8'bz;  // Controlled_Buffer_part controlled_buffer_2
  assign Output_Byte = Connect_Register_1_to_Bus ? Register_1_q : 8'bz;  // Controlled_Buffer_part controlled_buffer_3
  assign Output_Byte = Connect_Register_2_to_Bus ? Register_2_q : 8'bz;  // Controlled_Buffer_part controlled_buffer_4
  assign Output_Byte = Connect_Register_3_to_Bus ? Register_3_q : 8'bz;  // Controlled_Buffer_part controlled_buffer_5
endmodule

module BusTest (
  input  in_1,
  input  in_2,
  input  in_3,
  input  in_4,
  input  in_5,
  input  in_6,
  input  in_7,
  input  in_8,
  input  in_9,
  input  in_10,
  input  [7:0] in_11
);

  wire clock_1_out;
  wire [7:0] controlled_buffer_1_out, R1_q, R2_q, R3_q;

  Clock clock_1 (.out(clock_1_out));
  assign controlled_buffer_1_out = in_10 ? in_11 : 8'bz;  // Controlled_Buffer_part controlled_buffer_1
  Register R1 (.D(controlled_buffer_1_out), .en(in_2), .clk(clock_1_out), .Q(R1_q), .clr(in_3));
  Register R2 (.D(controlled_buffer_1_out), .en(in_5), .clk(clock_1_out), .Q(R2_q), .clr(in_6));
  Register R3 (.D(controlled_buffer_1_out), .en(in_8), .clk(clock_1_out), .Q(R3_q), .clr(in_9));
  assign controlled_buffer_1_out = in_1 ? R1_q : 8'bz;  // Controlled_Buffer_part controlled_buffer_2
  assign controlled_buffer_1_out = in_4 ? R2_q : 8'bz;  // Controlled_Buffer_part controlled_buffer_3
  assign controlled_buffer_1_out = in_7 ? R3_q : 8'bz;  // Controlled_Buffer_part controlled_buffer_4
  // Probe on controlled_buffer_1_out
endmodule

module Binary_to_Decimal_Decoder (
  input  [3:0] Binary_Input,
  output Decimal_Output_0,
  output Decimal_Output_1,
  output Decimal_Output_2,
  output Decimal_Output_3,
  output Decimal_Output_4,
  output Decimal_Output_5,
  output Decimal_Output_6,
  output Decimal_Output_7,
  output Decimal_Output_8,
  output Decimal_Output_9,
  output Decimal_Output_10,
  output Decimal_Output_11,
  output Decimal_Output_12,
  output Decimal_Output_13,
  output Decimal_Output_14,
  output Decimal_Output_15
);

  wire not_1_out, not_2_out, not_3_out, not_4_out;

  not not_1 (not_1_out, Binary_Input[3]);
  not not_2 (not_2_out, Binary_Input[2]);
  not not_3 (not_3_out, Binary_Input[1]);
  not not_4 (not_4_out, Binary_Input[0]);
  and and_1 (Decimal_Output_0, not_4_out, not_3_out, not_2_out, not_1_out);
  and and_2 (Decimal_Output_1, Binary_Input[0], not_3_out, not_2_out, not_1_out);
  and and_3 (Decimal_Output_2, not_4_out, Binary_Input[1], not_2_out, not_1_out);
  and and_4 (Decimal_Output_3, Binary_Input[0], Binary_Input[1], not_2_out, not_1_out);
  and and_5 (Decimal_Output_4, not_4_out, not_3_out, Binary_Input[2], not_1_out);
  and and_6 (Decimal_Output_5, Binary_Input[0], not_3_out, Binary_Input[2], not_1_out);
  and and_7 (Decimal_Output_6, not_4_out, Binary_Input[1], Binary_Input[2], not_1_out);
  and and_8 (Decimal_Output_7, Binary_Input[0], Binary_Input[1], Binary_Input[2], not_1_out);
  and and_9 (Decimal_Output_8, not_4_out, not_3_out, not_2_out, Binary_Input[3]);
  and and_10 (Decimal_Output_9, Binary_Input[0], not_3_out, not_2_out, Binary_Input[3]);
  and and_11 (Decimal_Output_10, not_4_out, Binary_Input[1], not_2_out, Binary_Input[3]);
  and and_12 (Decimal_Output_11, Binary_Input[0], Binary_Input[1], not_2_out, Binary_Input[3]);
  and and_13 (Decimal_Output_12, not_4_out, not_3_out, Binary_Input[2], Binary_Input[3]);
  and and_14 (Decimal_Output_13, Binary_Input[0], not_3_out, Binary_Input[2], Binary_Input[3]);
  and and_15 (Decimal_Output_14, not_4_out, Binary_Input[1], Binary_Input[2], Binary_Input[3]);
  and and_16 (Decimal_Output_15, Binary_Input[0], Binary_Input[1], Binary_Input[2], Binary_Input[3]);
endmodule

module Read_Only_Memory (
  input  [3:0] Address,
  input  Read_Enable,
  output [7:0] Data_Out
);

  wire and_1_out, and_2_out, and_3_out, and_4_out, and_5_out, and_6_out, and_7_out, and_8_out, and_9_out,
       and_10_out, and_11_out, and_12_out, and_13_out, and_14_out, and_15_out, and_16_out,
       controlled_buffer_1_out, controlled_buffer_17_out, controlled_buffer_33_out, controlled_buffer_49_out,
       controlled_buffer_65_out, controlled_buffer_81_out, controlled_buffer_101_out,
       controlled_buffer_119_out, d_ff_1_q, d_ff_2_q, d_ff_3_q, d_ff_4_q, d_ff_5_q, d_ff_6_q, d_ff_7_q,
       d_ff_8_q, d_ff_9_q, d_ff_10_q, d_ff_11_q, d_ff_12_q, d_ff_13_q, d_ff_14_q, d_ff_15_q, d_ff_16_q,
       d_ff_17_q, d_ff_18_q, d_ff_19_q, d_ff_20_q, d_ff_21_q, d_ff_22_q, d_ff_23_q, d_ff_24_q, d_ff_25_q,
       d_ff_26_q, d_ff_27_q, d_ff_28_q, d_ff_29_q, d_ff_30_q, d_ff_31_q, d_ff_32_q, d_ff_33_q, d_ff_34_q,
       d_ff_35_q, d_ff_36_q, d_ff_37_q, d_ff_38_q, d_ff_39_q, d_ff_40_q, d_ff_41_q, d_ff_42_q, d_ff_43_q,
       d_ff_44_q, d_ff_45_q, d_ff_46_q, d_ff_47_q, d_ff_48_q, d_ff_49_q, d_ff_50_q, d_ff_51_q, d_ff_52_q,
       d_ff_53_q, d_ff_54_q, d_ff_55_q, d_ff_56_q, d_ff_57_q, d_ff_58_q, d_ff_59_q, d_ff_60_q, d_ff_61_q,
       d_ff_62_q, d_ff_63_q, d_ff_64_q, d_ff_65_q, d_ff_66_q, d_ff_67_q, d_ff_68_q, d_ff_69_q, d_ff_70_q,
       d_ff_71_q, d_ff_72_q, d_ff_73_q, d_ff_74_q, d_ff_75_q, d_ff_76_q, d_ff_77_q, d_ff_78_q, d_ff_79_q,
       d_ff_80_q, d_ff_81_q, d_ff_82_q, d_ff_83_q, d_ff_84_q, d_ff_85_q, d_ff_86_q, d_ff_87_q, d_ff_88_q,
       d_ff_89_q, d_ff_90_q, d_ff_91_q, d_ff_92_q, d_ff_93_q, d_ff_94_q, d_ff_95_q, d_ff_96_q, d_ff_97_q,
       d_ff_98_q, d_ff_99_q, d_ff_100_q, d_ff_101_q, d_ff_102_q, d_ff_103_q, d_ff_104_q, d_ff_105_q,
       d_ff_106_q, d_ff_107_q, d_ff_108_q, d_ff_109_q, d_ff_110_q, d_ff_111_q, d_ff_112_q, d_ff_113_q,
       d_ff_114_q, d_ff_115_q, d_ff_116_q, d_ff_117_q, d_ff_118_q, d_ff_119_q, d_ff_120_q, d_ff_121_q,
       d_ff_122_q, d_ff_123_q, d_ff_124_q, d_ff_125_q, d_ff_126_q, d_ff_127_q, d_ff_128_q, not_1_out,
       not_2_out, not_3_out, not_4_out;

  not not_1 (not_1_out, Address[3]);
  not not_2 (not_2_out, Address[2]);
  not not_3 (not_3_out, Address[1]);
  not not_4 (not_4_out, Address[0]);
  and and_1 (and_1_out, not_4_out, not_3_out, not_2_out, not_1_out);
  D_Flip_Flop #(.trigger("high")) d_ff_1 (.Q(d_ff_1_q));  // open: D, clk, Qn, preset, reset
  and and_2 (and_2_out, Address[0], not_3_out, not_2_out, not_1_out);
  D_Flip_Flop #(.trigger("high")) d_ff_2 (.Q(d_ff_2_q));  // open: D, clk, Qn, preset, reset
  and and_3 (and_3_out, not_4_out, Address[1], not_2_out, not_1_out);
  D_Flip_Flop #(.trigger("high")) d_ff_3 (.Q(d_ff_3_q));  // open: D, clk, Qn, preset, reset
  and and_4 (and_4_out, Address[0], Address[1], not_2_out, not_1_out);
  D_Flip_Flop #(.trigger("high")) d_ff_4 (.Q(d_ff_4_q));  // open: D, clk, Qn, preset, reset
  and and_5 (and_5_out, not_4_out, not_3_out, Address[2], not_1_out);
  D_Flip_Flop #(.trigger("high")) d_ff_5 (.Q(d_ff_5_q));  // open: D, clk, Qn, preset, reset
  and and_6 (and_6_out, Address[0], not_3_out, Address[2], not_1_out);
  D_Flip_Flop #(.trigger("high")) d_ff_6 (.Q(d_ff_6_q));  // open: D, clk, Qn, preset, reset
  and and_7 (and_7_out, not_4_out, Address[1], Address[2], not_1_out);
  D_Flip_Flop #(.trigger("high")) d_ff_7 (.Q(d_ff_7_q));  // open: D, clk, Qn, preset, reset
  and and_8 (and_8_out, Address[0], Address[1], Address[2], not_1_out);
  D_Flip_Flop #(.trigger("high")) d_ff_8 (.Q(d_ff_8_q));  // open: D, clk, Qn, preset, reset
  and and_9 (and_9_out, not_4_out, not_3_out, not_2_out, Address[3]);
  D_Flip_Flop #(.trigger("high")) d_ff_9 (.Q(d_ff_9_q));  // open: D, clk, Qn, preset, reset
  and and_10 (and_10_out, Address[0], not_3_out, not_2_out, Address[3]);
  D_Flip_Flop #(.trigger("high")) d_ff_10 (.Q(d_ff_10_q));  // open: D, clk, Qn, preset, reset
  and and_11 (and_11_out, not_4_out, Address[1], not_2_out, Address[3]);
  D_Flip_Flop #(.trigger("high")) d_ff_11 (.Q(d_ff_11_q));  // open: D, clk, Qn, preset, reset
  and and_12 (and_12_out, Address[0], Address[1], not_2_out, Address[3]);
  D_Flip_Flop #(.trigger("high")) d_ff_12 (.Q(d_ff_12_q));  // open: D, clk, Qn, preset, reset
  and and_13 (and_13_out, not_4_out, not_3_out, Address[2], Address[3]);
  D_Flip_Flop #(.trigger("high")) d_ff_13 (.Q(d_ff_13_q));  // open: D, clk, Qn, preset, reset
  and and_14 (and_14_out, Address[0], not_3_out, Address[2], Address[3]);
  D_Flip_Flop #(.trigger("high")) d_ff_14 (.Q(d_ff_14_q));  // open: D, clk, Qn, preset, reset
  and and_15 (and_15_out, not_4_out, Address[1], Address[2], Address[3]);
  D_Flip_Flop #(.trigger("high")) d_ff_15 (.Q(d_ff_15_q));  // open: D, clk, Qn, preset, reset
  and and_16 (and_16_out, Address[0], Address[1], Address[2], Address[3]);
  D_Flip_Flop #(.trigger("high")) d_ff_16 (.Q(d_ff_16_q));  // open: D, clk, Qn, preset, reset
  assign controlled_buffer_1_out = and_1_out ? d_ff_1_q : 1'bz;  // Controlled_Buffer_part controlled_buffer_1
  assign controlled_buffer_1_out = and_2_out ? d_ff_2_q : 1'bz;  // Controlled_Buffer_part controlled_buffer_2
  assign controlled_buffer_1_out = and_3_out ? d_ff_3_q : 1'bz;  // Controlled_Buffer_part controlled_buffer_3
  assign controlled_buffer_1_out = and_4_out ? d_ff_4_q : 1'bz;  // Controlled_Buffer_part controlled_buffer_4
  assign controlled_buffer_1_out = and_5_out ? d_ff_5_q : 1'bz;  // Controlled_Buffer_part controlled_buffer_5
  assign controlled_buffer_1_out = and_6_out ? d_ff_6_q : 1'bz;  // Controlled_Buffer_part controlled_buffer_6
  assign controlled_buffer_1_out = and_7_out ? d_ff_7_q : 1'bz;  // Controlled_Buffer_part controlled_buffer_7
  assign controlled_buffer_1_out = and_8_out ? d_ff_8_q : 1'bz;  // Controlled_Buffer_part controlled_buffer_8
  assign controlled_buffer_1_out = and_9_out ? d_ff_9_q : 1'bz;  // Controlled_Buffer_part controlled_buffer_9
  assign controlled_buffer_1_out = and_10_out ? d_ff_10_q : 1'bz;  // Controlled_Buffer_part controlled_buffer_10
  assign controlled_buffer_1_out = and_11_out ? d_ff_11_q : 1'bz;  // Controlled_Buffer_part controlled_buffer_11
  assign controlled_buffer_1_out = and_12_out ? d_ff_12_q : 1'bz;  // Controlled_Buffer_part controlled_buffer_12
  assign controlled_buffer_1_out = and_13_out ? d_ff_13_q : 1'bz;  // Controlled_Buffer_part controlled_buffer_13
  assign controlled_buffer_1_out = and_14_out ? d_ff_14_q : 1'bz;  // Controlled_Buffer_part controlled_buffer_14
  assign controlled_buffer_1_out = and_15_out ? d_ff_15_q : 1'bz;  // Controlled_Buffer_part controlled_buffer_15
  assign controlled_buffer_1_out = and_16_out ? d_ff_16_q : 1'bz;  // Controlled_Buffer_part controlled_buffer_16
  D_Flip_Flop #(.trigger("high")) d_ff_17 (.Q(d_ff_17_q));  // open: D, clk, Qn, preset, reset
  D_Flip_Flop #(.trigger("high")) d_ff_18 (.Q(d_ff_18_q));  // open: D, clk, Qn, preset, reset
  D_Flip_Flop #(.trigger("high")) d_ff_19 (.Q(d_ff_19_q));  // open: D, clk, Qn, preset, reset
  D_Flip_Flop #(.trigger("high")) d_ff_20 (.Q(d_ff_20_q));  // open: D, clk, Qn, preset, reset
  D_Flip_Flop #(.trigger("high")) d_ff_21 (.Q(d_ff_21_q));  // open: D, clk, Qn, preset, reset
  D_Flip_Flop #(.trigger("high")) d_ff_22 (.Q(d_ff_22_q));  // open: D, clk, Qn, preset, reset
  D_Flip_Flop #(.trigger("high")) d_ff_23 (.Q(d_ff_23_q));  // open: D, clk, Qn, preset, reset
  D_Flip_Flop #(.trigger("high")) d_ff_24 (.Q(d_ff_24_q));  // open: D, clk, Qn, preset, reset
  D_Flip_Flop #(.trigger("high")) d_ff_25 (.Q(d_ff_25_q));  // open: D, clk, Qn, preset, reset
  D_Flip_Flop #(.trigger("high")) d_ff_26 (.Q(d_ff_26_q));  // open: D, clk, Qn, preset, reset
  D_Flip_Flop #(.trigger("high")) d_ff_27 (.Q(d_ff_27_q));  // open: D, clk, Qn, preset, reset
  D_Flip_Flop #(.trigger("high")) d_ff_28 (.Q(d_ff_28_q));  // open: D, clk, Qn, preset, reset
  D_Flip_Flop #(.trigger("high")) d_ff_29 (.Q(d_ff_29_q));  // open: D, clk, Qn, preset, reset
  D_Flip_Flop #(.trigger("high")) d_ff_30 (.Q(d_ff_30_q));  // open: D, clk, Qn, preset, reset
  D_Flip_Flop #(.trigger("high")) d_ff_31 (.Q(d_ff_31_q));  // open: D, clk, Qn, preset, reset
  D_Flip_Flop #(.trigger("high")) d_ff_32 (.Q(d_ff_32_q));  // open: D, clk, Qn, preset, reset
  D_Flip_Flop #(.trigger("high")) d_ff_33 (.Q(d_ff_33_q));  // open: D, clk, Qn, preset, reset
  assign controlled_buffer_17_out = and_1_out ? d_ff_17_q : 1'bz;  // Controlled_Buffer_part controlled_buffer_17
  D_Flip_Flop #(.trigger("high")) d_ff_34 (.Q(d_ff_34_q));  // open: D, clk, Qn, preset, reset
  assign controlled_buffer_17_out = and_2_out ? d_ff_18_q : 1'bz;  // Controlled_Buffer_part controlled_buffer_18
  D_Flip_Flop #(.trigger("high")) d_ff_35 (.Q(d_ff_35_q));  // open: D, clk, Qn, preset, reset
  assign controlled_buffer_17_out = and_3_out ? d_ff_19_q : 1'bz;  // Controlled_Buffer_part controlled_buffer_19
  D_Flip_Flop #(.trigger("high")) d_ff_36 (.Q(d_ff_36_q));  // open: D, clk, Qn, preset, reset
  assign controlled_buffer_17_out = and_4_out ? d_ff_20_q : 1'bz;  // Controlled_Buffer_part controlled_buffer_20
  D_Flip_Flop #(.trigger("high")) d_ff_37 (.Q(d_ff_37_q));  // open: D, clk, Qn, preset, reset
  assign controlled_buffer_17_out = and_5_out ? d_ff_21_q : 1'bz;  // Controlled_Buffer_part controlled_buffer_21
  D_Flip_Flop #(.trigger("high")) d_ff_38 (.Q(d_ff_38_q));  // open: D, clk, Qn, preset, reset
  assign controlled_buffer_17_out = and_6_out ? d_ff_22_q : 1'bz;  // Controlled_Buffer_part controlled_buffer_22
  D_Flip_Flop #(.trigger("high")) d_ff_39 (.Q(d_ff_39_q));  // open: D, clk, Qn, preset, reset
  assign controlled_buffer_17_out = and_7_out ? d_ff_23_q : 1'bz;  // Controlled_Buffer_part controlled_buffer_23
  D_Flip_Flop #(.trigger("high")) d_ff_40 (.Q(d_ff_40_q));  // open: D, clk, Qn, preset, reset
  assign controlled_buffer_17_out = and_8_out ? d_ff_24_q : 1'bz;  // Controlled_Buffer_part controlled_buffer_24
  D_Flip_Flop #(.trigger("high")) d_ff_41 (.Q(d_ff_41_q));  // open: D, clk, Qn, preset, reset
  assign controlled_buffer_17_out = and_9_out ? d_ff_25_q : 1'bz;  // Controlled_Buffer_part controlled_buffer_25
  D_Flip_Flop #(.trigger("high")) d_ff_42 (.Q(d_ff_42_q));  // open: D, clk, Qn, preset, reset
  assign controlled_buffer_17_out = and_10_out ? d_ff_26_q : 1'bz;  // Controlled_Buffer_part controlled_buffer_26
  D_Flip_Flop #(.trigger("high")) d_ff_43 (.Q(d_ff_43_q));  // open: D, clk, Qn, preset, reset
  assign controlled_buffer_17_out = and_11_out ? d_ff_27_q : 1'bz;  // Controlled_Buffer_part controlled_buffer_27
  D_Flip_Flop #(.trigger("high")) d_ff_44 (.Q(d_ff_44_q));  // open: D, clk, Qn, preset, reset
  assign controlled_buffer_17_out = and_12_out ? d_ff_28_q : 1'bz;  // Controlled_Buffer_part controlled_buffer_28
  D_Flip_Flop #(.trigger("high")) d_ff_45 (.Q(d_ff_45_q));  // open: D, clk, Qn, preset, reset
  assign controlled_buffer_17_out = and_13_out ? d_ff_29_q : 1'bz;  // Controlled_Buffer_part controlled_buffer_29
  D_Flip_Flop #(.trigger("high")) d_ff_46 (.Q(d_ff_46_q));  // open: D, clk, Qn, preset, reset
  assign controlled_buffer_17_out = and_14_out ? d_ff_30_q : 1'bz;  // Controlled_Buffer_part controlled_buffer_30
  D_Flip_Flop #(.trigger("high")) d_ff_47 (.Q(d_ff_47_q));  // open: D, clk, Qn, preset, reset
  assign controlled_buffer_17_out = and_15_out ? d_ff_31_q : 1'bz;  // Controlled_Buffer_part controlled_buffer_31
  D_Flip_Flop #(.trigger("high")) d_ff_48 (.Q(d_ff_48_q));  // open: D, clk, Qn, preset, reset
  assign controlled_buffer_17_out = and_16_out ? d_ff_32_q : 1'bz;  // Controlled_Buffer_part controlled_buffer_32
  assign controlled_buffer_33_out = and_1_out ? d_ff_33_q : 1'bz;  // Controlled_Buffer_part controlled_buffer_33
  assign controlled_buffer_33_out = and_2_out ? d_ff_34_q : 1'bz;  // Controlled_Buffer_part controlled_buffer_34
  assign controlled_buffer_33_out = and_3_out ? d_ff_35_q : 1'bz;  // Controlled_Buffer_part controlled_buffer_35
  assign controlled_buffer_33_out = and_4_out ? d_ff_36_q : 1'bz;  // Controlled_Buffer_part controlled_buffer_36
  assign controlled_buffer_33_out = and_5_out ? d_ff_37_q : 1'bz;  // Controlled_Buffer_part controlled_buffer_37
  assign controlled_buffer_33_out = and_6_out ? d_ff_38_q : 1'bz;  // Controlled_Buffer_part controlled_buffer_38
  assign controlled_buffer_33_out = and_7_out ? d_ff_39_q : 1'bz;  // Controlled_Buffer_part controlled_buffer_39
  assign controlled_buffer_33_out = and_8_out ? d_ff_40_q : 1'bz;  // Controlled_Buffer_part controlled_buffer_40
  assign controlled_buffer_33_out = and_9_out ? d_ff_41_q : 1'bz;  // Controlled_Buffer_part controlled_buffer_41
  assign controlled_buffer_33_out = and_10_out ? d_ff_42_q : 1'bz;  // Controlled_Buffer_part controlled_buffer_42
  assign controlled_buffer_33_out = and_11_out ? d_ff_43_q : 1'bz;  // Controlled_Buffer_part controlled_buffer_43
  assign controlled_buffer_33_out = and_12_out ? d_ff_44_q : 1'bz;  // Controlled_Buffer_part controlled_buffer_44
  assign controlled_buffer_33_out = and_13_out ? d_ff_45_q : 1'bz;  // Controlled_Buffer_part controlled_buffer_45
  assign controlled_buffer_33_out = and_14_out ? d_ff_46_q : 1'bz;  // Controlled_Buffer_part controlled_buffer_46
  assign controlled_buffer_33_out = and_15_out ? d_ff_47_q : 1'bz;  // Controlled_Buffer_part controlled_buffer_47
  assign controlled_buffer_33_out = and_16_out ? d_ff_48_q : 1'bz;  // Controlled_Buffer_part controlled_buffer_48
  D_Flip_Flop #(.trigger("high")) d_ff_49 (.Q(d_ff_49_q));  // open: D, clk, Qn, preset, reset
  D_Flip_Flop #(.trigger("high")) d_ff_50 (.Q(d_ff_50_q));  // open: D, clk, Qn, preset, reset
  D_Flip_Flop #(.trigger("high")) d_ff_51 (.Q(d_ff_51_q));  // open: D, clk, Qn, preset, reset
  D_Flip_Flop #(.trigger("high")) d_ff_52 (.Q(d_ff_52_q));  // open: D, clk, Qn, preset, reset
  D_Flip_Flop #(.trigger("high")) d_ff_53 (.Q(d_ff_53_q));  // open: D, clk, Qn, preset, reset
  D_Flip_Flop #(.trigger("high")) d_ff_54 (.Q(d_ff_54_q));  // open: D, clk, Qn, preset, reset
  D_Flip_Flop #(.trigger("high")) d_ff_55 (.Q(d_ff_55_q));  // open: D, clk, Qn, preset, reset
  D_Flip_Flop #(.trigger("high")) d_ff_56 (.Q(d_ff_56_q));  // open: D, clk, Qn, preset, reset
  D_Flip_Flop #(.trigger("high")) d_ff_57 (.Q(d_ff_57_q));  // open: D, clk, Qn, preset, reset
  D_Flip_Flop #(.trigger("high")) d_ff_58 (.Q(d_ff_58_q));  // open: D, clk, Qn, preset, reset
  D_Flip_Flop #(.trigger("high")) d_ff_59 (.Q(d_ff_59_q));  // open: D, clk, Qn, preset, reset
  D_Flip_Flop #(.trigger("high")) d_ff_60 (.Q(d_ff_60_q));  // open: D, clk, Qn, preset, reset
  D_Flip_Flop #(.trigger("high")) d_ff_61 (.Q(d_ff_61_q));  // open: D, clk, Qn, preset, reset
  D_Flip_Flop #(.trigger("high")) d_ff_62 (.Q(d_ff_62_q));  // open: D, clk, Qn, preset, reset
  D_Flip_Flop #(.trigger("high")) d_ff_63 (.Q(d_ff_63_q));  // open: D, clk, Qn, preset, reset
  D_Flip_Flop #(.trigger("high")) d_ff_64 (.Q(d_ff_64_q));  // open: D, clk, Qn, preset, reset
  D_Flip_Flop #(.trigger("high")) d_ff_65 (.Q(d_ff_65_q));  // open: D, clk, Qn, preset, reset
  assign controlled_buffer_49_out = and_1_out ? d_ff_49_q : 1'bz;  // Controlled_Buffer_part controlled_buffer_49
  D_Flip_Flop #(.trigger("high")) d_ff_66 (.Q(d_ff_66_q));  // open: D, clk, Qn, preset, reset
  assign controlled_buffer_49_out = and_2_out ? d_ff_50_q : 1'bz;  // Controlled_Buffer_part controlled_buffer_50
  D_Flip_Flop #(.trigger("high")) d_ff_67 (.Q(d_ff_67_q));  // open: D, clk, Qn, preset, reset
  assign controlled_buffer_49_out = and_3_out ? d_ff_51_q : 1'bz;  // Controlled_Buffer_part controlled_buffer_51
  D_Flip_Flop #(.trigger("high")) d_ff_68 (.Q(d_ff_68_q));  // open: D, clk, Qn, preset, reset
  assign controlled_buffer_49_out = and_4_out ? d_ff_52_q : 1'bz;  // Controlled_Buffer_part controlled_buffer_52
  D_Flip_Flop #(.trigger("high")) d_ff_69 (.Q(d_ff_69_q));  // open: D, clk, Qn, preset, reset
  assign controlled_buffer_49_out = and_5_out ? d_ff_53_q : 1'bz;  // Controlled_Buffer_part controlled_buffer_53
  D_Flip_Flop #(.trigger("high")) d_ff_70 (.Q(d_ff_70_q));  // open: D, clk, Qn, preset, reset
  assign controlled_buffer_49_out = and_6_out ? d_ff_54_q : 1'bz;  // Controlled_Buffer_part controlled_buffer_54
  D_Flip_Flop #(.trigger("high")) d_ff_71 (.Q(d_ff_71_q));  // open: D, clk, Qn, preset, reset
  assign controlled_buffer_49_out = and_7_out ? d_ff_55_q : 1'bz;  // Controlled_Buffer_part controlled_buffer_55
  D_Flip_Flop #(.trigger("high")) d_ff_72 (.Q(d_ff_72_q));  // open: D, clk, Qn, preset, reset
  assign controlled_buffer_49_out = and_8_out ? d_ff_56_q : 1'bz;  // Controlled_Buffer_part controlled_buffer_56
  D_Flip_Flop #(.trigger("high")) d_ff_73 (.Q(d_ff_73_q));  // open: D, clk, Qn, preset, reset
  assign controlled_buffer_49_out = and_9_out ? d_ff_57_q : 1'bz;  // Controlled_Buffer_part controlled_buffer_57
  D_Flip_Flop #(.trigger("high")) d_ff_74 (.Q(d_ff_74_q));  // open: D, clk, Qn, preset, reset
  assign controlled_buffer_49_out = and_10_out ? d_ff_58_q : 1'bz;  // Controlled_Buffer_part controlled_buffer_58
  D_Flip_Flop #(.trigger("high")) d_ff_75 (.Q(d_ff_75_q));  // open: D, clk, Qn, preset, reset
  assign controlled_buffer_49_out = and_11_out ? d_ff_59_q : 1'bz;  // Controlled_Buffer_part controlled_buffer_59
  D_Flip_Flop #(.trigger("high")) d_ff_76 (.Q(d_ff_76_q));  // open: D, clk, Qn, preset, reset
  assign controlled_buffer_49_out = and_12_out ? d_ff_60_q : 1'bz;  // Controlled_Buffer_part controlled_buffer_60
  D_Flip_Flop #(.trigger("high")) d_ff_77 (.Q(d_ff_77_q));  // open: D, clk, Qn, preset, reset
  assign controlled_buffer_49_out = and_13_out ? d_ff_61_q : 1'bz;  // Controlled_Buffer_part controlled_buffer_61
  D_Flip_Flop #(.trigger("high")) d_ff_78 (.Q(d_ff_78_q));  // open: D, clk, Qn, preset, reset
  assign controlled_buffer_49_out = and_14_out ? d_ff_62_q : 1'bz;  // Controlled_Buffer_part controlled_buffer_62
  D_Flip_Flop #(.trigger("high")) d_ff_79 (.Q(d_ff_79_q));  // open: D, clk, Qn, preset, reset
  assign controlled_buffer_49_out = and_15_out ? d_ff_63_q : 1'bz;  // Controlled_Buffer_part controlled_buffer_63
  D_Flip_Flop #(.trigger("high")) d_ff_80 (.Q(d_ff_80_q));  // open: D, clk, Qn, preset, reset
  assign controlled_buffer_49_out = and_16_out ? d_ff_64_q : 1'bz;  // Controlled_Buffer_part controlled_buffer_64
  assign controlled_buffer_65_out = and_1_out ? d_ff_65_q : 1'bz;  // Controlled_Buffer_part controlled_buffer_65
  assign controlled_buffer_65_out = and_2_out ? d_ff_66_q : 1'bz;  // Controlled_Buffer_part controlled_buffer_66
  assign controlled_buffer_65_out = and_3_out ? d_ff_67_q : 1'bz;  // Controlled_Buffer_part controlled_buffer_67
  assign controlled_buffer_65_out = and_4_out ? d_ff_68_q : 1'bz;  // Controlled_Buffer_part controlled_buffer_68
  assign controlled_buffer_65_out = and_5_out ? d_ff_69_q : 1'bz;  // Controlled_Buffer_part controlled_buffer_69
  assign controlled_buffer_65_out = and_6_out ? d_ff_70_q : 1'bz;  // Controlled_Buffer_part controlled_buffer_70
  assign controlled_buffer_65_out = and_7_out ? d_ff_71_q : 1'bz;  // Controlled_Buffer_part controlled_buffer_71
  assign controlled_buffer_65_out = and_8_out ? d_ff_72_q : 1'bz;  // Controlled_Buffer_part controlled_buffer_72
  assign controlled_buffer_65_out = and_9_out ? d_ff_73_q : 1'bz;  // Controlled_Buffer_part controlled_buffer_73
  assign controlled_buffer_65_out = and_10_out ? d_ff_74_q : 1'bz;  // Controlled_Buffer_part controlled_buffer_74
  assign controlled_buffer_65_out = and_11_out ? d_ff_75_q : 1'bz;  // Controlled_Buffer_part controlled_buffer_75
  assign controlled_buffer_65_out = and_12_out ? d_ff_76_q : 1'bz;  // Controlled_Buffer_part controlled_buffer_76
  assign controlled_buffer_65_out = and_13_out ? d_ff_77_q : 1'bz;  // Controlled_Buffer_part controlled_buffer_77
  assign controlled_buffer_65_out = and_14_out ? d_ff_78_q : 1'bz;  // Controlled_Buffer_part controlled_buffer_78
  assign controlled_buffer_65_out = and_15_out ? d_ff_79_q : 1'bz;  // Controlled_Buffer_part controlled_buffer_79
  assign controlled_buffer_65_out = and_16_out ? d_ff_80_q : 1'bz;  // Controlled_Buffer_part controlled_buffer_80
  D_Flip_Flop #(.trigger("high")) d_ff_81 (.Q(d_ff_81_q));  // open: D, clk, Qn, preset, reset
  D_Flip_Flop #(.trigger("high")) d_ff_82 (.Q(d_ff_82_q));  // open: D, clk, Qn, preset, reset
  D_Flip_Flop #(.trigger("high")) d_ff_83 (.Q(d_ff_83_q));  // open: D, clk, Qn, preset, reset
  D_Flip_Flop #(.trigger("high")) d_ff_84 (.Q(d_ff_84_q));  // open: D, clk, Qn, preset, reset
  D_Flip_Flop #(.trigger("high")) d_ff_85 (.Q(d_ff_85_q));  // open: D, clk, Qn, preset, reset
  D_Flip_Flop #(.trigger("high")) d_ff_86 (.Q(d_ff_86_q));  // open: D, clk, Qn, preset, reset
  D_Flip_Flop #(.trigger("high")) d_ff_87 (.Q(d_ff_87_q));  // open: D, clk, Qn, preset, reset
  D_Flip_Flop #(.trigger("high")) d_ff_88 (.Q(d_ff_88_q));  // open: D, clk, Qn, preset, reset
  D_Flip_Flop #(.trigger("high")) d_ff_89 (.Q(d_ff_89_q));  // open: D, clk, Qn, preset, reset
  D_Flip_Flop #(.trigger("high")) d_ff_90 (.Q(d_ff_90_q));  // open: D, clk, Qn, preset, reset
  D_Flip_Flop #(.trigger("high")) d_ff_91 (.Q(d_ff_91_q));  // open: D, clk, Qn, preset, reset
  D_Flip_Flop #(.trigger("high")) d_ff_92 (.Q(d_ff_92_q));  // open: D, clk, Qn, preset, reset
  D_Flip_Flop #(.trigger("high")) d_ff_93 (.Q(d_ff_93_q));  // open: D, clk, Qn, preset, reset
  D_Flip_Flop #(.trigger("high")) d_ff_94 (.Q(d_ff_94_q));  // open: D, clk, Qn, preset, reset
  D_Flip_Flop #(.trigger("high")) d_ff_95 (.Q(d_ff_95_q));  // open: D, clk, Qn, preset, reset
  D_Flip_Flop #(.trigger("high")) d_ff_96 (.Q(d_ff_96_q));  // open: D, clk, Qn, preset, reset
  assign controlled_buffer_81_out = and_1_out ? d_ff_81_q : 1'bz;  // Controlled_Buffer_part controlled_buffer_81
  assign controlled_buffer_81_out = and_2_out ? d_ff_82_q : 1'bz;  // Controlled_Buffer_part controlled_buffer_82
  assign controlled_buffer_81_out = and_3_out ? d_ff_83_q : 1'bz;  // Controlled_Buffer_part controlled_buffer_83
  assign controlled_buffer_81_out = and_4_out ? d_ff_84_q : 1'bz;  // Controlled_Buffer_part controlled_buffer_84
  assign controlled_buffer_81_out = and_5_out ? d_ff_85_q : 1'bz;  // Controlled_Buffer_part controlled_buffer_85
  assign controlled_buffer_81_out = and_6_out ? d_ff_86_q : 1'bz;  // Controlled_Buffer_part controlled_buffer_86
  assign controlled_buffer_81_out = and_7_out ? d_ff_87_q : 1'bz;  // Controlled_Buffer_part controlled_buffer_87
  assign controlled_buffer_81_out = and_8_out ? d_ff_88_q : 1'bz;  // Controlled_Buffer_part controlled_buffer_88
  assign controlled_buffer_81_out = and_9_out ? d_ff_89_q : 1'bz;  // Controlled_Buffer_part controlled_buffer_89
  assign controlled_buffer_81_out = and_10_out ? d_ff_90_q : 1'bz;  // Controlled_Buffer_part controlled_buffer_90
  assign controlled_buffer_81_out = and_11_out ? d_ff_91_q : 1'bz;  // Controlled_Buffer_part controlled_buffer_91
  assign controlled_buffer_81_out = and_12_out ? d_ff_92_q : 1'bz;  // Controlled_Buffer_part controlled_buffer_92
  assign controlled_buffer_81_out = and_13_out ? d_ff_93_q : 1'bz;  // Controlled_Buffer_part controlled_buffer_93
  assign controlled_buffer_81_out = and_14_out ? d_ff_94_q : 1'bz;  // Controlled_Buffer_part controlled_buffer_94
  assign controlled_buffer_81_out = and_15_out ? d_ff_95_q : 1'bz;  // Controlled_Buffer_part controlled_buffer_95
  assign controlled_buffer_81_out = and_16_out ? d_ff_96_q : 1'bz;  // Controlled_Buffer_part controlled_buffer_96
  assign Data_Out[6] = Read_Enable ? controlled_buffer_17_out : 1'bz;  // Controlled_Buffer_part controlled_buffer_97
  assign Data_Out[7] = Read_Enable ? controlled_buffer_1_out : 1'bz;  // Controlled_Buffer_part controlled_buffer_98
  D_Flip_Flop #(.trigger("high")) d_ff_97 (.Q(d_ff_97_q));  // open: D, clk, Qn, preset, reset
  D_Flip_Flop #(.trigger("high")) d_ff_98 (.Q(d_ff_98_q));  // open: D, clk, Qn, preset, reset
  D_Flip_Flop #(.trigger("high")) d_ff_99 (.Q(d_ff_99_q));  // open: D, clk, Qn, preset, reset
  D_Flip_Flop #(.trigger("high")) d_ff_100 (.Q(d_ff_100_q));  // open: D, clk, Qn, preset, reset
  D_Flip_Flop #(.trigger("high")) d_ff_101 (.Q(d_ff_101_q));  // open: D, clk, Qn, preset, reset
  D_Flip_Flop #(.trigger("high")) d_ff_102 (.Q(d_ff_102_q));  // open: D, clk, Qn, preset, reset
  D_Flip_Flop #(.trigger("high")) d_ff_103 (.Q(d_ff_103_q));  // open: D, clk, Qn, preset, reset
  D_Flip_Flop #(.trigger("high")) d_ff_104 (.Q(d_ff_104_q));  // open: D, clk, Qn, preset, reset
  D_Flip_Flop #(.trigger("high")) d_ff_105 (.Q(d_ff_105_q));  // open: D, clk, Qn, preset, reset
  D_Flip_Flop #(.trigger("high")) d_ff_106 (.Q(d_ff_106_q));  // open: D, clk, Qn, preset, reset
  D_Flip_Flop #(.trigger("high")) d_ff_107 (.Q(d_ff_107_q));  // open: D, clk, Qn, preset, reset
  D_Flip_Flop #(.trigger("high")) d_ff_108 (.Q(d_ff_108_q));  // open: D, clk, Qn, preset, reset
  D_Flip_Flop #(.trigger("high")) d_ff_109 (.Q(d_ff_109_q));  // open: D, clk, Qn, preset, reset
  D_Flip_Flop #(.trigger("high")) d_ff_110 (.Q(d_ff_110_q));  // open: D, clk, Qn, preset, reset
  D_Flip_Flop #(.trigger("high")) d_ff_111 (.Q(d_ff_111_q));  // open: D, clk, Qn, preset, reset
  D_Flip_Flop #(.trigger("high")) d_ff_112 (.Q(d_ff_112_q));  // open: D, clk, Qn, preset, reset
  assign Data_Out[4] = Read_Enable ? controlled_buffer_49_out : 1'bz;  // Controlled_Buffer_part controlled_buffer_99
  assign Data_Out[5] = Read_Enable ? controlled_buffer_33_out : 1'bz;  // Controlled_Buffer_part controlled_buffer_100
  D_Flip_Flop #(.trigger("high")) d_ff_113 (.Q(d_ff_113_q));  // open: D, clk, Qn, preset, reset
  assign controlled_buffer_101_out = and_1_out ? d_ff_97_q : 1'bz;  // Controlled_Buffer_part controlled_buffer_101
  D_Flip_Flop #(.trigger("high")) d_ff_114 (.Q(d_ff_114_q));  // open: D, clk, Qn, preset, reset
  assign controlled_buffer_101_out = and_2_out ? d_ff_98_q : 1'bz;  // Controlled_Buffer_part controlled_buffer_102
  D_Flip_Flop #(.trigger("high")) d_ff_115 (.Q(d_ff_115_q));  // open: D, clk, Qn, preset, reset
  assign controlled_buffer_101_out = and_3_out ? d_ff_99_q : 1'bz;  // Controlled_Buffer_part controlled_buffer_103
  D_Flip_Flop #(.trigger("high")) d_ff_116 (.Q(d_ff_116_q));  // open: D, clk, Qn, preset, reset
  assign controlled_buffer_101_out = and_4_out ? d_ff_100_q : 1'bz;  // Controlled_Buffer_part controlled_buffer_104
  D_Flip_Flop #(.trigger("high")) d_ff_117 (.Q(d_ff_117_q));  // open: D, clk, Qn, preset, reset
  assign controlled_buffer_101_out = and_5_out ? d_ff_101_q : 1'bz;  // Controlled_Buffer_part controlled_buffer_105
  D_Flip_Flop #(.trigger("high")) d_ff_118 (.Q(d_ff_118_q));  // open: D, clk, Qn, preset, reset
  assign controlled_buffer_101_out = and_6_out ? d_ff_102_q : 1'bz;  // Controlled_Buffer_part controlled_buffer_106
  D_Flip_Flop #(.trigger("high")) d_ff_119 (.Q(d_ff_119_q));  // open: D, clk, Qn, preset, reset
  assign controlled_buffer_101_out = and_7_out ? d_ff_103_q : 1'bz;  // Controlled_Buffer_part controlled_buffer_107
  D_Flip_Flop #(.trigger("high")) d_ff_120 (.Q(d_ff_120_q));  // open: D, clk, Qn, preset, reset
  assign controlled_buffer_101_out = and_8_out ? d_ff_104_q : 1'bz;  // Controlled_Buffer_part controlled_buffer_108
  D_Flip_Flop #(.trigger("high")) d_ff_121 (.Q(d_ff_121_q));  // open: D, clk, Qn, preset, reset
  assign controlled_buffer_101_out = and_9_out ? d_ff_105_q : 1'bz;  // Controlled_Buffer_part controlled_buffer_109
  D_Flip_Flop #(.trigger("high")) d_ff_122 (.Q(d_ff_122_q));  // open: D, clk, Qn, preset, reset
  assign controlled_buffer_101_out = and_10_out ? d_ff_106_q : 1'bz;  // Controlled_Buffer_part controlled_buffer_110
  D_Flip_Flop #(.trigger("high")) d_ff_123 (.Q(d_ff_123_q));  // open: D, clk, Qn, preset, reset
  assign controlled_buffer_101_out = and_11_out ? d_ff_107_q : 1'bz;  // Controlled_Buffer_part controlled_buffer_111
  D_Flip_Flop #(.trigger("high")) d_ff_124 (.Q(d_ff_124_q));  // open: D, clk, Qn, preset, reset
  assign controlled_buffer_101_out = and_12_out ? d_ff_108_q : 1'bz;  // Controlled_Buffer_part controlled_buffer_112
  D_Flip_Flop #(.trigger("high")) d_ff_125 (.Q(d_ff_125_q));  // open: D, clk, Qn, preset, reset
  assign controlled_buffer_101_out = and_13_out ? d_ff_109_q : 1'bz;  // Controlled_Buffer_part controlled_buffer_113
  D_Flip_Flop #(.trigger("high")) d_ff_126 (.Q(d_ff_126_q));  // open: D, clk, Qn, preset, reset
  assign controlled_buffer_101_out = and_14_out ? d_ff_110_q : 1'bz;  // Controlled_Buffer_part controlled_buffer_114
  D_Flip_Flop #(.trigger("high")) d_ff_127 (.Q(d_ff_127_q));  // open: D, clk, Qn, preset, reset
  assign controlled_buffer_101_out = and_15_out ? d_ff_111_q : 1'bz;  // Controlled_Buffer_part controlled_buffer_115
  D_Flip_Flop #(.trigger("high")) d_ff_128 (.Q(d_ff_128_q));  // open: D, clk, Qn, preset, reset
  assign controlled_buffer_101_out = and_16_out ? d_ff_112_q : 1'bz;  // Controlled_Buffer_part controlled_buffer_116
  assign Data_Out[2] = Read_Enable ? controlled_buffer_81_out : 1'bz;  // Controlled_Buffer_part controlled_buffer_117
  assign Data_Out[3] = Read_Enable ? controlled_buffer_65_out : 1'bz;  // Controlled_Buffer_part controlled_buffer_118
  assign controlled_buffer_119_out = and_1_out ? d_ff_113_q : 1'bz;  // Controlled_Buffer_part controlled_buffer_119
  assign controlled_buffer_119_out = and_2_out ? d_ff_114_q : 1'bz;  // Controlled_Buffer_part controlled_buffer_120
  assign controlled_buffer_119_out = and_3_out ? d_ff_115_q : 1'bz;  // Controlled_Buffer_part controlled_buffer_121
  assign controlled_buffer_119_out = and_4_out ? d_ff_116_q : 1'bz;  // Controlled_Buffer_part controlled_buffer_122
  assign controlled_buffer_119_out = and_5_out ? d_ff_117_q : 1'bz;  // Controlled_Buffer_part controlled_buffer_123
  assign controlled_buffer_119_out = and_6_out ? d_ff_118_q : 1'bz;  // Controlled_Buffer_part controlled_buffer_124
  assign controlled_buffer_119_out = and_7_out ? d_ff_119_q : 1'bz;  // Controlled_Buffer_part controlled_buffer_125
  assign controlled_buffer_119_out = and_8_out ? d_ff_120_q : 1'bz;  // Controlled_Buffer_part controlled_buffer_126
  assign controlled_buffer_119_out = and_9_out ? d_ff_121_q : 1'bz;  // Controlled_Buffer_part controlled_buffer_127
  assign controlled_buffer_119_out = and_10_out ? d_ff_122_q : 1'bz;  // Controlled_Buffer_part controlled_buffer_128
  assign controlled_buffer_119_out = and_11_out ? d_ff_123_q : 1'bz;  // Controlled_Buffer_part controlled_buffer_129
  assign controlled_buffer_119_out = and_12_out ? d_ff_124_q : 1'bz;  // Controlled_Buffer_part controlled_buffer_130
  assign controlled_buffer_119_out = and_13_out ? d_ff_125_q : 1'bz;  // Controlled_Buffer_part controlled_buffer_131
  assign controlled_buffer_119_out = and_14_out ? d_ff_126_q : 1'bz;  // Controlled_Buffer_part controlled_buffer_132
  assign controlled_buffer_119_out = and_15_out ? d_ff_127_q : 1'bz;  // Controlled_Buffer_part controlled_buffer_133
  assign controlled_buffer_119_out = and_16_out ? d_ff_128_q : 1'bz;  // Controlled_Buffer_part controlled_buffer_134
  assign Data_Out[0] = Read_Enable ? controlled_buffer_119_out : 1'bz;  // Controlled_Buffer_part controlled_buffer_135
  assign Data_Out[1] = Read_Enable ? controlled_buffer_101_out : 1'bz;  // Controlled_Buffer_part controlled_buffer_136
endmodule

module Random_Access_Memory (
  input  [7:0] Address,
  input  [7:0] Input_Data,
  input  Write_Enable,
  input  Read_Enable,
  output [7:0] Output_Data
);

  wire not_1_out, not_2_out, or_1_out, Read, Write;
  wire [7:0] ram_1_dout;

  not not_1 (not_1_out, Read_Enable);
  not not_2 (not_2_out, Write_Enable);
  LED led_1 (.in(Write));
  and and_1 (Write, Write_Enable, not_1_out);
  LED led_2 (.in(Read));
  and and_2 (Read, not_2_out, Read_Enable);
  or or_1 (or_1_out, Read, Write);
  RAM #(.trigger("high")) ram_1 (.addr(Address), .we(Write), .oe(Read), .din(Input_Data), .dout(ram_1_dout));
  Two_Digit_Hexadecimal_Display_With_Enable_Bit two_digit_hexadecimal_display_with_enable_bit_1 (
    .Byte(Address), .Enable(or_1_out));
  assign Output_Data = Read ? ram_1_dout : 8'bz;  // Controlled_Buffer_part controlled_buffer_1
  Two_Digit_Hexadecimal_Display_With_Enable_Bit two_digit_hexadecimal_display_with_enable_bit_2 (
    .Byte(Input_Data), .Enable(Write));
  Two_Digit_Hexadecimal_Display_With_Enable_Bit two_digit_hexadecimal_display_with_enable_bit_3 (
    .Byte(Output_Data), .Enable(Read));
endmodule

module Byte_Bus (
  input  [7:0] Byte
);

  wire seven_segment_display_driver_1_a, seven_segment_display_driver_1_b, seven_segment_display_driver_1_c,
       seven_segment_display_driver_1_d, seven_segment_display_driver_1_e, seven_segment_display_driver_1_f,
       seven_segment_display_driver_1_g, seven_segment_display_driver_2_a, seven_segment_display_driver_2_b,
       seven_segment_display_driver_2_c, seven_segment_display_driver_2_d, seven_segment_display_driver_2_e,
       seven_segment_display_driver_2_f, seven_segment_display_driver_2_g;

  Seven_Segment_Display_Driver seven_segment_display_driver_1 (
    .Bit_0(Byte[0]), .Bit_1(Byte[1]), .Bit_2(Byte[2]), .Bit_3(Byte[3]), .B(seven_segment_display_driver_1_b),
    .A(seven_segment_display_driver_1_a), .F(seven_segment_display_driver_1_f),
    .G(seven_segment_display_driver_1_g), .E(seven_segment_display_driver_1_e),
    .D(seven_segment_display_driver_1_d), .C(seven_segment_display_driver_1_c));  // open: Decimal_Point, DP
  Seven_Segment_Display_Driver seven_segment_display_driver_2 (
    .Bit_0(Byte[4]), .Bit_1(Byte[5]), .Bit_2(Byte[6]), .Bit_3(Byte[7]), .B(seven_segment_display_driver_2_b),
    .A(seven_segment_display_driver_2_a), .F(seven_segment_display_driver_2_f),
    .G(seven_segment_display_driver_2_g), .E(seven_segment_display_driver_2_e),
    .D(seven_segment_display_driver_2_d), .C(seven_segment_display_driver_2_c));  // open: Decimal_Point, DP
  _7_Segment_Display u_7_segment_display_1 (
    .g(seven_segment_display_driver_2_g), .f(seven_segment_display_driver_2_f),
    .a(seven_segment_display_driver_2_a), .b(seven_segment_display_driver_2_b),
    .e(seven_segment_display_driver_2_e), .d(seven_segment_display_driver_2_d),
    .c(seven_segment_display_driver_2_c));  // open: dp
  _7_Segment_Display u_7_segment_display_2 (
    .g(seven_segment_display_driver_1_g), .f(seven_segment_display_driver_1_f),
    .a(seven_segment_display_driver_1_a), .b(seven_segment_display_driver_1_b),
    .e(seven_segment_display_driver_1_e), .d(seven_segment_display_driver_1_d),
    .c(seven_segment_display_driver_1_c));  // open: dp
endmodule

module Register_Bank (
  input  [7:0] Data_Input,
  input  Write_Enable,
  input  Write_Selector,
  input  Read_Enable,
  input  Read_Selector,
  input  CLK,
  input  Reset,
  output [7:0] Data_Output,
  output [7:0] Register_A_Output,
  output [7:0] Register_B_Output
);

  wire and_1_out, and_2_out, and_3_out, and_4_out, not_1_out, not_2_out;

  not not_1 (not_1_out, Write_Selector);
  not not_2 (not_2_out, Read_Selector);
  LED led_1 (.in(and_1_out));
  and and_1 (and_1_out, Write_Enable, not_1_out);
  LED led_2 (.in(and_2_out));
  and and_2 (and_2_out, Write_Enable, Write_Selector);
  LED led_3 (.in(and_3_out));
  and and_3 (and_3_out, Read_Enable, not_2_out);
  LED led_4 (.in(and_4_out));
  and and_4 (and_4_out, Read_Enable, Read_Selector);
  Register register_1 (.D(Data_Input), .en(and_1_out), .clk(CLK), .Q(Register_A_Output), .clr(Reset));
  Register register_2 (.D(Data_Input), .en(and_2_out), .clk(CLK), .Q(Register_B_Output), .clr(Reset));
  assign Data_Output = and_3_out ? Register_A_Output : 8'bz;  // Controlled_Buffer_part controlled_buffer_1
  assign Data_Output = and_4_out ? Register_B_Output : 8'bz;  // Controlled_Buffer_part controlled_buffer_2
  Two_Digit_Hexadecimal_Display two_digit_hexadecimal_display_1 (.Byte(Register_A_Output));
  Two_Digit_Hexadecimal_Display two_digit_hexadecimal_display_2 (.Byte(Register_B_Output));
endmodule

module Memory_Address_Register (
  input  [7:0] Input_Data,
  input  Write_Enable,
  input  CLK,
  input  Reset,
  output [7:0] Output_Data
);

  Register MAR (.D(Input_Data), .en(Write_Enable), .clk(CLK), .Q(Output_Data), .clr(Reset));
  Two_Digit_Hexadecimal_Display two_digit_hexadecimal_display_1 (.Byte(Output_Data));
endmodule

module Output_Register (
  input  [7:0] Data,
  input  Write_Enable,
  input  CLK,
  input  Reset
);

  wire [7:0] Output_Register_q;

  Register Output_Register (.D(Data), .en(Write_Enable), .clk(CLK), .Q(Output_Register_q), .clr(Reset));
  Three_Digit_Decimal_Integer_Display three_digit_decimal_integer_display_1 (.Binary_Number(Output_Register_q));
endmodule

module Instruction_Register (
  input  [7:0] Input_Data,
  input  Instruction_Write_Enable,
  input  Immediate_Write_Enable,
  input  CLK,
  input  Reset,
  input  Read_Immediate,
  output [7:0] Opcode,
  output [7:0] Output_Data
);

  wire and_1_out, and_2_out, d_ff_1_q, not_1_out, not_2_out, or_1_out;
  wire [7:0] Immediate_q;

  not not_1 (not_1_out, Immediate_Write_Enable);
  not not_2 (not_2_out, Instruction_Write_Enable);
  and and_1 (and_1_out, Instruction_Write_Enable, not_1_out);
  and and_2 (and_2_out, not_2_out, Immediate_Write_Enable);
  Register Instruction (.D(Input_Data), .en(and_1_out), .clk(CLK), .Q(Opcode), .clr(Reset));
  Register Immediate (.D(Input_Data), .en(and_2_out), .clk(CLK), .Q(Immediate_q), .clr(or_1_out));
  or or_1 (or_1_out, and_1_out, Reset);
  Two_Digit_Hexadecimal_Display two_digit_hexadecimal_display_1 (.Byte(Opcode));
  assign Output_Data = Read_Immediate ? Immediate_q : 8'bz;  // Controlled_Buffer_part controlled_buffer_1
  Two_Digit_Hexadecimal_Display_With_Enable_Bit two_digit_hexadecimal_display_with_enable_bit_1 (
    .Byte(Immediate_q), .Enable(d_ff_1_q));
  D_Flip_Flop d_ff_1 (.Q(d_ff_1_q), .preset(and_2_out), .reset(or_1_out));  // open: clk, D, Qn
endmodule

module Program_Counter (
  input  Reset,
  input  Jump,
  input  Increment,
  input  CLK,
  input  [7:0] Jump_Address,
  input  Read_Enable,
  output Overflow,
  output [7:0] Address
);

  wire [7:0] counter_1_q;

  Counter counter_1 (
    .clr(Reset), .load(Jump), .up(1'b1), .count(Increment), .clk(CLK), .D(Jump_Address), .carry(Overflow),
    .Q(counter_1_q));
  assign Address = Read_Enable ? counter_1_q : 8'bz;  // Controlled_Buffer_part controlled_buffer_1
  Two_Digit_Hexadecimal_Display two_digit_hexadecimal_display_1 (.Byte(counter_1_q));
endmodule
module Control_Unit (
  input  CLK,
  input  Reset,
  input  [7:0] Instruction,
  input  [2:0] Flags,
  output PC_INC,
  output PC_WE,
  output PC_RE,
  output IRIN_WE,
  output IRIN_RE,
  output IRIM_WE,
  output IRIM_RE,
  output MAR_WE,
  output RAM_WE,
  output RAM_RE,
  output RB_WE,
  output RB_WS,
  output RB_RE,
  output RB_RS,
  output OUT_WE,
  output ALU_RE,
  output [2:0] ALU_OP
);

  wire and_1_out, BCC_out, BCS_out, BEQ_out, BMI_out, BNE_out, BPL_out, BRK, CF, d_ff_1_q, d_ff_13_q, HLT,
       JMP_out, JUMP, NF, not_1_out, not_2_out, not_3_out, not_4_out, not_5_out, not_6_out, not_7_out,
       not_8_out, not_9_out, not_10_out, not_11_out, not_12_out, not_13_out, not_14_out, not_15_out,
       not_16_out, not_17_out, not_18_out, not_19_out, not_20_out, not_21_out, not_22_out, not_23_out,
       not_24_out, not_25_out, not_26_out, not_27_out, not_28_out, not_29_out, not_30_out, not_31_out,
       not_32_out, not_33_out, not_34_out, not_35_out, not_36_out, not_37_out, not_38_out, not_39_out,
       not_40_out, not_41_out, not_42_out, or_3_out, Reset_t, T0, T1, T2, T3, T4, T5, T6, T7, T8, T9, T10,
       undriven, ZF;
  wire [2:0] priority_encoder_1_out;
  wire [3:3] undriven_2;
  wire [29:1] controlled_buffer_1_out;
  wire [31:0] rom_1_data;

  D_Flip_Flop #(.trigger("high")) d_ff_1 (.Q(d_ff_1_q), .preset(HLT), .reset(Reset));  // open: D, clk, Qn
  D_Flip_Flop #(.trigger("falling")) d_ff_2 (
    .D(d_ff_13_q), .clk(CLK), .Q(T0), .preset(Reset_t), .reset(d_ff_1_q));  // open: Qn
  D_Flip_Flop #(.trigger("falling")) d_ff_3 (.D(T0), .clk(CLK), .Q(T1), .reset(Reset_t));  // open: Qn, preset
  or or_1 (Reset_t, d_ff_1_q, Reset, BRK);
  not not_1 (not_1_out, Instruction[0]);
  not not_2 (not_2_out, Instruction[3]);
  not not_3 (not_3_out, Instruction[4]);
  not not_4 (not_4_out, Instruction[5]);
  not not_5 (not_5_out, Instruction[6]);
  not not_6 (not_6_out, Instruction[7]);
  not not_7 (not_7_out, Instruction[0]);
  not not_8 (not_8_out, Instruction[2]);
  not not_9 (not_9_out, Instruction[3]);
  not not_10 (not_10_out, Instruction[5]);
  not not_11 (not_11_out, Instruction[6]);
  not not_12 (not_12_out, Instruction[7]);
  not not_13 (not_13_out, Instruction[2]);
  not not_14 (not_14_out, Instruction[3]);
  not not_15 (not_15_out, Instruction[5]);
  not not_16 (not_16_out, Instruction[6]);
  not not_17 (not_17_out, Instruction[7]);
  not not_18 (not_18_out, ZF);
  not not_19 (not_19_out, Instruction[0]);
  not not_20 (not_20_out, Instruction[1]);
  not not_21 (not_21_out, Instruction[3]);
  not not_22 (not_22_out, Instruction[5]);
  not not_23 (not_23_out, Instruction[6]);
  not not_24 (not_24_out, Instruction[7]);
  not not_25 (not_25_out, NF);
  not not_26 (not_26_out, Instruction[1]);
  not not_27 (not_27_out, Instruction[3]);
  not not_28 (not_28_out, Instruction[5]);
  not not_29 (not_29_out, Instruction[6]);
  not not_30 (not_30_out, Instruction[7]);
  not not_31 (not_31_out, Instruction[0]);
  not not_32 (not_32_out, Instruction[3]);
  not not_33 (not_33_out, Instruction[5]);
  not not_34 (not_34_out, Instruction[6]);
  not not_35 (not_35_out, Instruction[7]);
  not not_36 (not_36_out, Instruction[3]);
  not not_37 (not_37_out, Instruction[5]);
  not not_38 (not_38_out, Instruction[6]);
  not not_39 (not_39_out, Instruction[7]);
  not not_40 (not_40_out, CF);
  D_Flip_Flop #(.trigger("falling")) d_ff_4 (.D(T1), .clk(CLK), .Q(T2), .reset(Reset_t));  // open: Qn, preset
  Priority_Encoder priority_encoder_1 (
    .in0(T2), .in1(T3), .in2(T4), .in3(T5), .in4(T6), .in5(T7), .in6(T8), .in7(T9),
    .out(priority_encoder_1_out));  // open: en_in, gs, en_out
  Two_Digit_Hexadecimal_Display two_digit_hexadecimal_display_1 (.Byte(Instruction));
  and JMP (JMP_out, not_1_out, Instruction[1], Instruction[2], not_2_out, not_3_out, not_4_out, not_5_out, not_6_out);
  and BEQ (BEQ_out, not_7_out, Instruction[1], not_8_out, not_9_out, Instruction[4], not_10_out, not_11_out, not_12_out, ZF);
  and BNE (BNE_out, Instruction[0], Instruction[1], not_13_out, not_14_out, Instruction[4], not_15_out, not_16_out, not_17_out, not_18_out);
  and BPL (BPL_out, not_19_out, not_20_out, Instruction[2], not_21_out, Instruction[4], not_22_out, not_23_out, not_24_out, not_25_out);
  and BMI (BMI_out, Instruction[0], not_26_out, Instruction[2], not_27_out, Instruction[4], not_28_out, not_29_out, not_30_out, NF);
  and BCS (BCS_out, not_31_out, Instruction[1], Instruction[2], not_32_out, Instruction[4], not_33_out, not_34_out, not_35_out, CF);
  and BCC (BCC_out, Instruction[0], Instruction[1], Instruction[2], not_36_out, Instruction[4], not_37_out, not_38_out, not_39_out, not_40_out);
  ROM #(.addrWidth(11), .dataWidth(32)) rom_1 (.addr({Instruction, priority_encoder_1_out}), .data(rom_1_data));
  D_Flip_Flop #(.trigger("falling")) d_ff_5 (.D(T2), .clk(CLK), .Q(T3), .reset(Reset_t));  // open: Qn, preset
  or or_2 (JUMP, JMP_out, BEQ_out, BNE_out, BPL_out, BMI_out, BCS_out, BCC_out);
  D_Flip_Flop #(.trigger("falling")) d_ff_6 (.D(T3), .clk(CLK), .Q(T4), .reset(Reset_t));  // open: Qn, preset
  D_Flip_Flop #(.trigger("falling")) d_ff_7 (.D(T4), .clk(CLK), .Q(T5), .reset(Reset_t));  // open: Qn, preset
  or or_3 (or_3_out, T2, T3, T4, T5, T6, T7, T8, T9, T10);
  D_Flip_Flop #(.trigger("falling")) d_ff_8 (.D(T5), .clk(CLK), .Q(T6), .reset(Reset_t));  // open: Qn, preset
  assign {HLT, BRK, controlled_buffer_1_out[29:19], ALU_OP, ALU_RE, OUT_WE, RB_RS, RB_RE, RB_WS, RB_WE, RAM_RE, RAM_WE, MAR_WE, IRIM_RE, IRIM_WE, IRIN_RE, IRIN_WE, PC_RE, controlled_buffer_1_out[1], PC_INC} = T0 ? 32'h84 : 32'bz;  // Controlled_Buffer_part controlled_buffer_1
  assign {HLT, BRK, controlled_buffer_1_out[29:19], ALU_OP, ALU_RE, OUT_WE, RB_RS, RB_RE, RB_WS, RB_WE, RAM_RE, RAM_WE, MAR_WE, IRIM_RE, IRIM_WE, IRIN_RE, IRIN_WE, PC_RE, controlled_buffer_1_out[1], PC_INC} = T1 ? 32'h209 : 32'bz;  // Controlled_Buffer_part controlled_buffer_2
  assign {HLT, BRK, controlled_buffer_1_out[29:19], ALU_OP, ALU_RE, OUT_WE, RB_RS, RB_RE, RB_WS, RB_WE, RAM_RE, RAM_WE, MAR_WE, IRIM_RE, IRIM_WE, IRIN_RE, IRIN_WE, PC_RE, controlled_buffer_1_out[1], PC_INC} = and_1_out ? rom_1_data : 32'bz;  // Controlled_Buffer_part controlled_buffer_3
  and and_1 (and_1_out, or_3_out, not_41_out, not_42_out);
  not not_41 (not_41_out, T0);
  not not_42 (not_42_out, T1);
  Register #(.width(3)) register_1 (.D(Flags), .en(ALU_RE), .clk(CLK), .Q({CF, NF, ZF}), .clr(undriven));
  D_Flip_Flop #(.trigger("falling")) d_ff_9 (.D(T6), .clk(CLK), .Q(T7), .reset(Reset_t));  // open: Qn, preset
  LED PC_INC_Light (.in(PC_INC));
  LED PC_RE_Light (.in(PC_RE));
  LED IRIN_WE_Light (.in(IRIN_WE));
  LED IRIN_RE_Light (.in(IRIN_RE));
  LED IRIM_WE_Light (.in(IRIM_WE));
  LED IRIM_RE_Light (.in(IRIM_RE));
  LED MAR_WE_Light (.in(MAR_WE));
  LED RAM_WE_Light (.in(RAM_WE));
  LED RAM_RE_Light (.in(RAM_RE));
  LED RB_WE_Light (.in(RB_WE));
  LED RB_WS_Light (.in(RB_WS));
  LED RB_RE_Light (.in(RB_RE));
  LED RB_RS_Light (.in(RB_RS));
  LED OUT_WE_Light (.in(OUT_WE));
  LED ALU_RE_Light (.in(ALU_RE));
  D_Flip_Flop #(.trigger("falling")) d_ff_10 (.D(T7), .clk(CLK), .Q(T8), .reset(Reset_t));  // open: Qn, preset
  One_Digit_Hexadecimal_Display one_digit_hexadecimal_display_1 (.Nibble({undriven_2[3], ALU_OP}));
  D_Flip_Flop #(.trigger("falling")) d_ff_11 (.D(T8), .clk(CLK), .Q(T9), .reset(Reset_t));  // open: Qn, preset
  and and_2 (PC_WE, JUMP, controlled_buffer_1_out[1]);
  D_Flip_Flop #(.trigger("falling")) d_ff_12 (.D(T9), .clk(CLK), .Q(T10), .reset(Reset_t));  // open: Qn, preset
  LED PC_WE_Light (.in(PC_WE));
  D_Flip_Flop #(.trigger("falling")) d_ff_13 (.D(T10), .clk(CLK), .Q(d_ff_13_q), .reset(Reset_t));  // open: Qn, preset

  // Notes on the sheet:
  //   contents of rom_1 (hex, n*v repeats v):
  //   40000000 7*80000000 84 221 440 40000000 4*80000000 84 221 c0 600 40000000 80000000 80000000 80000000
  //   84 221 c0 e00 8400 40000000 80000000 80000000 84 221 c0 e00 18400 40000000 80000000 80000000 84 221
  //   c0 1100 40000000 80000000 80000000 80000000 84 221 42 40000000 4*80000000 84 221 c40 68400 40000000
  //   80000000 80000000 80000000 84 221 c0 e00 68400 40000000 80000000 80000000 78400 40000000 6*80000000
  //   5000 40000000 6*80000000 84 221 c40 48400 40000000 80000000 80000000 80000000 84 221 c0 e00 48400
  //   40000000 80000000 80000000 84 221 c40 58400 40000000 80000000 80000000 80000000 84 221 c0 e00 58400
  //   40000000 80000000 80000000 84 221 c40 8400 40000000 80000000 80000000 80000000 28400 40000000
  //   6*80000000 38400 40000000 6*80000000 84 221 42 40000000 4*80000000 84 221 42 40000000 4*80000000 84
  //   221 42 40000000 4*80000000 84 221 42 40000000 4*80000000 84 221 42 40000000 4*80000000 84 221 42
  //   40000000 4*80000000 84 221 c40 18400 40000000 80000000 80000000 80000000 40000000 7*80000000
  //   40000000 7*80000000 40000000 7*80000000 40000000 7*80000000 40000000 7*80000000 40000000 7*80000000
  //   40000000 7*80000000 40000000 7*80000000 40000000 7*80000000 40000000 7*80000000 40000000 7*80000000
  //   40000000 7*80000000 40000000 7*80000000 40000000 7*80000000 40000000 7*80000000 40000000 7*80000000
  //   40000000 7*80000000 40000000 7*80000000 40000000 7*80000000 40000000 7*80000000 40000000 7*80000000
  //   40000000 7*80000000 40000000 7*80000000 40000000 7*80000000 40000000 7*80000000 40000000 7*80000000
  //   40000000 7*80000000 40000000 7*80000000 40000000 7*80000000 40000000 7*80000000 40000000 7*80000000
  //   40000000 7*80000000 40000000 7*80000000 40000000 7*80000000 40000000 7*80000000 40000000 7*80000000
  //   40000000 7*80000000 40000000 7*80000000 40000000 7*80000000 40000000 7*80000000 40000000 7*80000000
  //   40000000 7*80000000 40000000 7*80000000 40000000 7*80000000 40000000 7*80000000 40000000 7*80000000
  //   40000000 7*80000000 40000000 7*80000000 40000000 7*80000000 40000000 7*80000000 40000000 7*80000000
  //   40000000 7*80000000 40000000 7*80000000 40000000 7*80000000 40000000 7*80000000 40000000 7*80000000
  //   40000000 7*80000000 40000000 7*80000000 40000000 7*80000000 40000000 7*80000000 40000000 7*80000000
  //   40000000 7*80000000 40000000 7*80000000 40000000 7*80000000 40000000 7*80000000 40000000 7*80000000
  //   40000000 7*80000000 40000000 7*80000000 40000000 7*80000000 40000000 7*80000000 40000000 7*80000000
  //   40000000 7*80000000 40000000 7*80000000 40000000 7*80000000 40000000 7*80000000 40000000 7*80000000
  //   40000000 7*80000000 40000000 7*80000000 40000000 7*80000000 40000000 7*80000000 40000000 7*80000000
  //   40000000 7*80000000 40000000 7*80000000 40000000 7*80000000 40000000 7*80000000 40000000 7*80000000
  //   40000000 7*80000000 40000000 7*80000000 40000000 7*80000000 40000000 7*80000000 40000000 7*80000000
  //   40000000 7*80000000 40000000 7*80000000 40000000 7*80000000 40000000 7*80000000 40000000 7*80000000
  //   40000000 7*80000000 40000000 7*80000000 40000000 7*80000000 40000000 7*80000000 40000000 7*80000000
  //   40000000 7*80000000 40000000 7*80000000 40000000 7*80000000 40000000 7*80000000 40000000 7*80000000
  //   40000000 7*80000000 40000000 7*80000000 40000000 7*80000000 40000000 7*80000000 40000000 7*80000000
  //   40000000 7*80000000 40000000 7*80000000 40000000 7*80000000 40000000 7*80000000 40000000 7*80000000
  //   40000000 7*80000000 40000000 7*80000000 40000000 7*80000000 40000000 7*80000000 40000000 7*80000000
  //   40000000 7*80000000 40000000 7*80000000 40000000 7*80000000 40000000 7*80000000 40000000 7*80000000
  //   40000000 7*80000000 40000000 7*80000000 40000000 7*80000000 40000000 7*80000000 40000000 7*80000000
  //   40000000 7*80000000 40000000 7*80000000 40000000 7*80000000 40000000 7*80000000 40000000 7*80000000
  //   40000000 7*80000000 40000000 7*80000000 40000000 7*80000000 40000000 7*80000000 40000000 7*80000000
  //   40000000 7*80000000 40000000 7*80000000 40000000 7*80000000 40000000 7*80000000 40000000 7*80000000
  //   40000000 7*80000000 40000000 7*80000000 40000000 7*80000000 40000000 7*80000000 40000000 7*80000000
  //   40000000 7*800000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
endmodule

module Computer (
  input  in_1
);

  wire CLK, control_unit_1_alu_re, control_unit_1_irim_re, control_unit_1_irim_we, control_unit_1_irin_we,
       control_unit_1_mar_we, control_unit_1_out_we, control_unit_1_pc_inc, control_unit_1_pc_re,
       control_unit_1_pc_we, control_unit_1_ram_re, control_unit_1_ram_we, control_unit_1_rb_re,
       control_unit_1_rb_rs, control_unit_1_rb_we, control_unit_1_rb_ws;
  wire [2:0] alu_1_flags, control_unit_1_alu_op;
  wire [7:0] instruction_register_1_opcode, instruction_register_1_output_data,
       memory_address_register_1_output_data, register_bank_1_register_a_output,
       register_bank_1_register_b_output;

  Byte_Bus byte_bus_1 (.Byte(instruction_register_1_output_data));
  Clock clock_1 (.out(CLK));
  Instruction_Register instruction_register_1 (
    .Instruction_Write_Enable(control_unit_1_irin_we), .Immediate_Write_Enable(control_unit_1_irim_we),
    .CLK(CLK), .Reset(in_1), .Read_Immediate(control_unit_1_irim_re),
    .Input_Data(instruction_register_1_output_data), .Output_Data(instruction_register_1_output_data),
    .Opcode(instruction_register_1_opcode));
  Control_Unit control_unit_1 (
    .CLK(CLK), .Reset(in_1), .Instruction(instruction_register_1_opcode), .Flags(alu_1_flags),
    .PC_WE(control_unit_1_pc_we), .RB_RS(control_unit_1_rb_rs), .OUT_WE(control_unit_1_out_we),
    .ALU_RE(control_unit_1_alu_re), .PC_INC(control_unit_1_pc_inc), .PC_RE(control_unit_1_pc_re),
    .IRIN_WE(control_unit_1_irin_we), .IRIM_WE(control_unit_1_irim_we), .IRIM_RE(control_unit_1_irim_re),
    .MAR_WE(control_unit_1_mar_we), .RAM_WE(control_unit_1_ram_we), .RAM_RE(control_unit_1_ram_re),
    .RB_WE(control_unit_1_rb_we), .RB_WS(control_unit_1_rb_ws), .RB_RE(control_unit_1_rb_re),
    .ALU_OP(control_unit_1_alu_op));  // open: IRIN_RE
  Register_Bank register_bank_1 (
    .Write_Enable(control_unit_1_rb_we), .Write_Selector(control_unit_1_rb_ws),
    .Read_Enable(control_unit_1_rb_re), .Read_Selector(control_unit_1_rb_rs), .CLK(CLK), .Reset(in_1),
    .Data_Input(instruction_register_1_output_data), .Register_A_Output(register_bank_1_register_a_output),
    .Register_B_Output(register_bank_1_register_b_output), .Data_Output(instruction_register_1_output_data));
  ALU alu_1 (
    .Read_Enable(control_unit_1_alu_re), .Opcode(control_unit_1_alu_op),
    .A(register_bank_1_register_a_output), .B(register_bank_1_register_b_output),
    .Result(instruction_register_1_output_data), .Flags(alu_1_flags));  // open: Carry_In
  Program_Counter program_counter_1 (
    .CLK(CLK), .Read_Enable(control_unit_1_pc_re), .Reset(in_1), .Jump(control_unit_1_pc_we),
    .Increment(control_unit_1_pc_inc), .Jump_Address(instruction_register_1_output_data),
    .Address(instruction_register_1_output_data));  // open: Overflow
  Memory_Address_Register memory_address_register_1 (
    .Write_Enable(control_unit_1_mar_we), .CLK(CLK), .Reset(in_1),
    .Input_Data(instruction_register_1_output_data), .Output_Data(memory_address_register_1_output_data));
  Output_Register output_register_1 (
    .Write_Enable(control_unit_1_out_we), .CLK(CLK), .Reset(in_1), .Data(instruction_register_1_output_data));
  Random_Access_Memory random_access_memory_1 (
    .Write_Enable(control_unit_1_ram_we), .Read_Enable(control_unit_1_ram_re),
    .Address(memory_address_register_1_output_data), .Input_Data(instruction_register_1_output_data),
    .Output_Data(instruction_register_1_output_data));

  // Other names for the same wires on the sheet: Reset = in_1
endmodule
